// Logisim project CPU MIPS 16 BITS FINAL COM DISPLAY.circ as structural Verilog: 14 circuits, main circuit main
// ll
module main (
  input  ON_OFF
);

  wire CLOCK_out, cpu_1_read_mem, cpu_1_write_mem, RESET_out, show_1_a0, show_1_a1, show_1_a2, show_1_a3,
       show_1_a4, show_1_a5, show_1_a6, show_1_b0, show_1_b1, show_1_b2, show_1_b3, show_1_b4, show_1_b5,
       show_1_b6, show_1_c0, show_1_c1, show_1_c2, show_1_c3, show_1_c4, show_1_c5, show_1_c6, show_2_a0,
       show_2_a1, show_2_a2, show_2_a3, show_2_a4, show_2_a5, show_2_a6, show_2_b0, show_2_b1, show_2_b2,
       show_2_b3, show_2_b4, show_2_b5, show_2_b6, show_2_c0, show_2_c1, show_2_c2, show_2_c3, show_2_c4,
       show_2_c5, show_2_c6, show_3_a0, show_3_a1, show_3_a2, show_3_a3, show_3_a4, show_3_a5, show_3_a6,
       show_3_b0, show_3_b1, show_3_b2, show_3_b3, show_3_b4, show_3_b5, show_3_b6, show_3_c0, show_3_c1,
       show_3_c2, show_3_c3, show_3_c4, show_3_c5, show_3_c6, show_4_a0, show_4_a1, show_4_a2, show_4_a3,
       show_4_a4, show_4_a5, show_4_a6, show_4_b0, show_4_b1, show_4_b2, show_4_b3, show_4_b4, show_4_b5,
       show_4_b6, show_4_c0, show_4_c1, show_4_c2, show_4_c3, show_4_c4, show_4_c5, show_4_c6, show_5_a0,
       show_5_a1, show_5_a2, show_5_a3, show_5_a4, show_5_a5, show_5_a6, show_5_b0, show_5_b1, show_5_b2,
       show_5_b3, show_5_b4, show_5_b5, show_5_b6, show_5_c0, show_5_c1, show_5_c2, show_5_c3, show_5_c4,
       show_5_c5, show_5_c6, show_6_a0, show_6_a1, show_6_a2, show_6_a3, show_6_a4, show_6_a5, show_6_a6,
       show_6_b0, show_6_b1, show_6_b2, show_6_b3, show_6_b4, show_6_b5, show_6_b6, show_6_c0, show_6_c1,
       show_6_c2, show_6_c3, show_6_c4, show_6_c5, show_6_c6, show_7_a0, show_7_a1, show_7_a2, show_7_a3,
       show_7_a4, show_7_a5, show_7_a6, show_7_b0, show_7_b1, show_7_b2, show_7_b3, show_7_b4, show_7_b5,
       show_7_b6, show_7_c0, show_7_c1, show_7_c2, show_7_c3, show_7_c4, show_7_c5, show_7_c6;
  wire [3:0] show_instr_1_mais_sign, show_instr_1_menos_sign, show_instr_1_out_3, show_instr_1_out_4,
       show_instr_1_out_5, show_instr_1_out_6, show_instr_1_out_7, show_instr_1_out_8, show_instr_1_out_9,
       show_instr_1_out_10, show_instr_1_out_11, show_instr_1_out_12, show_instr_1_out_13,
       show_instr_1_out_14, show_instr_1_out_15, show_instr_1_out_16;
  wire [7:0] D0, D1, S0, S1, S2, T0, T1;
  wire [15:0] INSTR;

  LED READ (.in(cpu_1_read_mem));
  Button RESET (.out(RESET_out));
  Hex_Digit_Display hex_digit_display_1 (.value(show_instr_1_mais_sign));  // open: dp
  Hex_Digit_Display hex_digit_display_2 (.value(show_instr_1_out_3));  // open: dp
  SHOW_INSTR show_instr_1 (
    .Input(INSTR), .mais_sign(show_instr_1_mais_sign), .out_3(show_instr_1_out_3),
    .out_4(show_instr_1_out_4), .out_5(show_instr_1_out_5), .out_6(show_instr_1_out_6),
    .out_7(show_instr_1_out_7), .out_8(show_instr_1_out_8), .out_9(show_instr_1_out_9),
    .out_10(show_instr_1_out_10), .out_11(show_instr_1_out_11), .out_12(show_instr_1_out_12),
    .out_13(show_instr_1_out_13), .out_14(show_instr_1_out_14), .out_15(show_instr_1_out_15),
    .out_16(show_instr_1_out_16), .menos_sign(show_instr_1_menos_sign));
  LED WRITE (.in(cpu_1_write_mem));
  CPU cpu_1 (
    .ON_OFF(ON_OFF), .RESET(RESET_out), .CLOCK(CLOCK_out), .WRITE_MEM(cpu_1_write_mem),
    .READ_MEM(cpu_1_read_mem), .INSTRUCTION(INSTR), .S0(S0), .S1(S1), .S2(S2), .D1(D1), .T0(T0), .T1(T1),
    .D0(D0));
  Hex_Digit_Display hex_digit_display_3 (.value(show_instr_1_out_4));  // open: dp
  Hex_Digit_Display hex_digit_display_4 (.value(show_instr_1_out_5));  // open: dp
  Clock CLOCK (.out(CLOCK_out));
  Hex_Digit_Display hex_digit_display_5 (.value(show_instr_1_out_7));  // open: dp
  Hex_Digit_Display hex_digit_display_6 (.value(show_instr_1_out_6));  // open: dp
  Hex_Digit_Display hex_digit_display_7 (.value(show_instr_1_out_9));  // open: dp
  Hex_Digit_Display hex_digit_display_8 (.value(show_instr_1_out_8));  // open: dp
  Hex_Digit_Display hex_digit_display_9 (.value(show_instr_1_out_10));  // open: dp
  Hex_Digit_Display hex_digit_display_10 (.value(show_instr_1_out_11));  // open: dp
  _7_Segment_Display u_7_segment_display_1 (
    .g(show_1_a3), .f(show_1_a2), .a(show_1_a1), .b(show_1_a0), .e(show_1_a4), .d(show_1_a5), .c(show_1_a6));  // open: dp
  _7_Segment_Display u_7_segment_display_2 (
    .g(show_1_b3), .f(show_1_b2), .a(show_1_b1), .b(show_1_b0), .e(show_1_b4), .d(show_1_b5), .c(show_1_b6));  // open: dp
  _7_Segment_Display u_7_segment_display_3 (
    .g(show_2_a3), .f(show_2_a2), .a(show_2_a1), .b(show_2_a0), .e(show_2_a4), .d(show_2_a5), .c(show_2_a6));  // open: dp
  _7_Segment_Display u_7_segment_display_4 (
    .g(show_2_b3), .f(show_2_b2), .a(show_2_b1), .b(show_2_b0), .e(show_2_b4), .d(show_2_b5), .c(show_2_b6));  // open: dp
  _7_Segment_Display u_7_segment_display_5 (
    .g(show_3_a3), .f(show_3_a2), .a(show_3_a1), .b(show_3_a0), .e(show_3_a4), .d(show_3_a5), .c(show_3_a6));  // open: dp
  _7_Segment_Display u_7_segment_display_6 (
    .g(show_3_b3), .f(show_3_b2), .a(show_3_b1), .b(show_3_b0), .e(show_3_b4), .d(show_3_b5), .c(show_3_b6));  // open: dp
  Hex_Digit_Display hex_digit_display_11 (.value(show_instr_1_out_12));  // open: dp
  Hex_Digit_Display hex_digit_display_12 (.value(show_instr_1_out_13));  // open: dp
  SHOW show_1 (
    .IN(S0), .A1(show_1_a1), .A0(show_1_a0), .A6(show_1_a6), .A5(show_1_a5), .A4(show_1_a4), .A2(show_1_a2),
    .A3(show_1_a3), .B1(show_1_b1), .B0(show_1_b0), .B6(show_1_b6), .B5(show_1_b5), .B4(show_1_b4),
    .B2(show_1_b2), .B3(show_1_b3), .C1(show_1_c1), .C0(show_1_c0), .C6(show_1_c6), .C5(show_1_c5),
    .C4(show_1_c4), .C2(show_1_c2), .C3(show_1_c3));
  _7_Segment_Display u_7_segment_display_7 (
    .g(show_1_c3), .f(show_1_c2), .a(show_1_c1), .b(show_1_c0), .e(show_1_c4), .d(show_1_c5), .c(show_1_c6));  // open: dp
  SHOW show_2 (
    .IN(S1), .A1(show_2_a1), .A0(show_2_a0), .A6(show_2_a6), .A5(show_2_a5), .A4(show_2_a4), .A2(show_2_a2),
    .A3(show_2_a3), .B1(show_2_b1), .B0(show_2_b0), .B6(show_2_b6), .B5(show_2_b5), .B4(show_2_b4),
    .B2(show_2_b2), .B3(show_2_b3), .C1(show_2_c1), .C0(show_2_c0), .C6(show_2_c6), .C5(show_2_c5),
    .C4(show_2_c4), .C2(show_2_c2), .C3(show_2_c3));
  _7_Segment_Display u_7_segment_display_8 (
    .g(show_2_c3), .f(show_2_c2), .a(show_2_c1), .b(show_2_c0), .e(show_2_c4), .d(show_2_c5), .c(show_2_c6));  // open: dp
  SHOW show_3 (
    .IN(S2), .A1(show_3_a1), .A0(show_3_a0), .A6(show_3_a6), .A5(show_3_a5), .A4(show_3_a4), .A2(show_3_a2),
    .A3(show_3_a3), .B1(show_3_b1), .B0(show_3_b0), .B6(show_3_b6), .B5(show_3_b5), .B4(show_3_b4),
    .B2(show_3_b2), .B3(show_3_b3), .C1(show_3_c1), .C0(show_3_c0), .C6(show_3_c6), .C5(show_3_c5),
    .C4(show_3_c4), .C2(show_3_c2), .C3(show_3_c3));
  _7_Segment_Display u_7_segment_display_9 (
    .g(show_3_c3), .f(show_3_c2), .a(show_3_c1), .b(show_3_c0), .e(show_3_c4), .d(show_3_c5), .c(show_3_c6));  // open: dp
  Hex_Digit_Display hex_digit_display_13 (.value(show_instr_1_out_14));  // open: dp
  _7_Segment_Display u_7_segment_display_10 (
    .g(show_4_a3), .f(show_4_a2), .a(show_4_a1), .b(show_4_a0), .e(show_4_a4), .d(show_4_a5), .c(show_4_a6));  // open: dp
  _7_Segment_Display u_7_segment_display_11 (
    .g(show_5_a3), .f(show_5_a2), .a(show_5_a1), .b(show_5_a0), .e(show_5_a4), .d(show_5_a5), .c(show_5_a6));  // open: dp
  Hex_Digit_Display hex_digit_display_14 (.value(show_instr_1_out_16));  // open: dp
  Hex_Digit_Display hex_digit_display_15 (.value(show_instr_1_out_15));  // open: dp
  _7_Segment_Display u_7_segment_display_12 (
    .g(show_4_b3), .f(show_4_b2), .a(show_4_b1), .b(show_4_b0), .e(show_4_b4), .d(show_4_b5), .c(show_4_b6));  // open: dp
  _7_Segment_Display u_7_segment_display_13 (
    .g(show_4_c3), .f(show_4_c2), .a(show_4_c1), .b(show_4_c0), .e(show_4_c4), .d(show_4_c5), .c(show_4_c6));  // open: dp
  _7_Segment_Display u_7_segment_display_14 (
    .g(show_5_c3), .f(show_5_c2), .a(show_5_c1), .b(show_5_c0), .e(show_5_c4), .d(show_5_c5), .c(show_5_c6));  // open: dp
  _7_Segment_Display u_7_segment_display_15 (
    .g(show_5_b3), .f(show_5_b2), .a(show_5_b1), .b(show_5_b0), .e(show_5_b4), .d(show_5_b5), .c(show_5_b6));  // open: dp
  Hex_Digit_Display hex_digit_display_16 (.value(show_instr_1_menos_sign));  // open: dp
  SHOW show_4 (
    .IN(T0), .A1(show_4_a1), .A0(show_4_a0), .A6(show_4_a6), .A5(show_4_a5), .A4(show_4_a4), .A2(show_4_a2),
    .A3(show_4_a3), .B1(show_4_b1), .B0(show_4_b0), .B6(show_4_b6), .B5(show_4_b5), .B4(show_4_b4),
    .B2(show_4_b2), .B3(show_4_b3), .C1(show_4_c1), .C0(show_4_c0), .C6(show_4_c6), .C5(show_4_c5),
    .C4(show_4_c4), .C2(show_4_c2), .C3(show_4_c3));
  SHOW show_5 (
    .IN(T1), .A1(show_5_a1), .A0(show_5_a0), .A6(show_5_a6), .A5(show_5_a5), .A4(show_5_a4), .A2(show_5_a2),
    .A3(show_5_a3), .B1(show_5_b1), .B0(show_5_b0), .B6(show_5_b6), .B5(show_5_b5), .B4(show_5_b4),
    .B2(show_5_b2), .B3(show_5_b3), .C1(show_5_c1), .C0(show_5_c0), .C6(show_5_c6), .C5(show_5_c5),
    .C4(show_5_c4), .C2(show_5_c2), .C3(show_5_c3));
  _7_Segment_Display u_7_segment_display_16 (
    .g(show_6_a3), .f(show_6_a2), .a(show_6_a1), .b(show_6_a0), .e(show_6_a4), .d(show_6_a5), .c(show_6_a6));  // open: dp
  _7_Segment_Display u_7_segment_display_17 (
    .g(show_7_a3), .f(show_7_a2), .a(show_7_a1), .b(show_7_a0), .e(show_7_a4), .d(show_7_a5), .c(show_7_a6));  // open: dp
  _7_Segment_Display u_7_segment_display_18 (
    .g(show_6_c3), .f(show_6_c2), .a(show_6_c1), .b(show_6_c0), .e(show_6_c4), .d(show_6_c5), .c(show_6_c6));  // open: dp
  _7_Segment_Display u_7_segment_display_19 (
    .g(show_6_b3), .f(show_6_b2), .a(show_6_b1), .b(show_6_b0), .e(show_6_b4), .d(show_6_b5), .c(show_6_b6));  // open: dp
  _7_Segment_Display u_7_segment_display_20 (
    .g(show_7_c3), .f(show_7_c2), .a(show_7_c1), .b(show_7_c0), .e(show_7_c4), .d(show_7_c5), .c(show_7_c6));  // open: dp
  _7_Segment_Display u_7_segment_display_21 (
    .g(show_7_b3), .f(show_7_b2), .a(show_7_b1), .b(show_7_b0), .e(show_7_b4), .d(show_7_b5), .c(show_7_b6));  // open: dp
  SHOW show_6 (
    .IN(D0), .A1(show_6_a1), .A0(show_6_a0), .A6(show_6_a6), .A5(show_6_a5), .A4(show_6_a4), .A2(show_6_a2),
    .A3(show_6_a3), .B1(show_6_b1), .B0(show_6_b0), .B6(show_6_b6), .B5(show_6_b5), .B4(show_6_b4),
    .B2(show_6_b2), .B3(show_6_b3), .C1(show_6_c1), .C0(show_6_c0), .C6(show_6_c6), .C5(show_6_c5),
    .C4(show_6_c4), .C2(show_6_c2), .C3(show_6_c3));
  SHOW show_7 (
    .IN(D1), .A1(show_7_a1), .A0(show_7_a0), .A6(show_7_a6), .A5(show_7_a5), .A4(show_7_a4), .A2(show_7_a2),
    .A3(show_7_a3), .B1(show_7_b1), .B0(show_7_b0), .B6(show_7_b6), .B5(show_7_b5), .B4(show_7_b4),
    .B2(show_7_b2), .B3(show_7_b3), .C1(show_7_c1), .C0(show_7_c0), .C6(show_7_c6), .C5(show_7_c5),
    .C4(show_7_c4), .C2(show_7_c2), .C3(show_7_c3));

  // Notes on the sheet:
  //   INSTRUÇÃO
  //   REGISTRADORES
endmodule

// count
module COUNT (
  input  [3:0] plus_1,
  input  Enable,
  input  Clear,
  input  Clock,
  output [3:0] Out
);

  wire [3:0] adder_1_out;

  Adder #(.width(4)) adder_1 (.a(Out), .b(plus_1), .out(adder_1_out));  // open: cin, cout
  Register #(.width(4)) register_1 (.D(adder_1_out), .en(Enable), .Q(Out), .clk(Clock), .clr(Clear));
endmodule

module CONTROLLER (
  input  on_off,
  input  [7:0] load_mem_data,
  input  [3:0] pc_out,
  input  [15:0] data_instr,
  input  Reset,
  input  CLOCK,
  input  [7:0] alu_out,
  input  [7:0] r1_out,
  input  [7:0] r2_out,
  output [7:0] write_mem_data,
  output [7:0] mem_data_adrress,
  output mem_s_r,
  output mem_cl,
  output cpi_en,
  output pc_en,
  output pc_cl,
  output [3:0] pc_in,
  output r_en,
  output r_cl,
  output [7:0] alu_a,
  output [7:0] alu_b,
  output [2:0] alu_op,
  output alu_en,
  output [2:0] r1_select,
  output [2:0] r2_select,
  output [2:0] r_data_select,
  output REG_EN_WRITE,
  output [7:0] REG_DATA,
  output regs_cl
);

  wire adder_1_cout, and_1_out, and_2_out, and_3_out, comparator_1_eq, comparator_2_lt, DMX_r2_out, I_011,
       I_100, I_101, I_110, J_111, MUX_r1_select, MUX_r2_select, MUX_r_data_select, MUX_ula_b, MUX_ula_op,
       nor_1_out, nor_5_out, not_2_out, not_3_out, or_1_out, or_4_out, R_000, R_001, R_010, REG_ULA_EN,
       SHIFT_R;
  wire [1:0] MUX_I, MUX_R, MUX_reg_data;
  wire [2:0] FUNC_R, RD_R, RS_I, RS_R, RT_I, RT_R;
  wire [3:0] adder_1_out, ADDR_J, bit_extender_3_out;
  wire [7:0] A_B, IMM_I, R2_OUT_B, RESULT_LESS, RESULT_SHIFT;
  wire [15:0] demultiplexer_1_out0, demultiplexer_1_out1, demultiplexer_1_out2, demultiplexer_1_out3,
       demultiplexer_1_out4, demultiplexer_1_out5, demultiplexer_1_out6, demultiplexer_1_out7,
       multiplexer_6_out;
  wire [15:13] multiplexer_5_out;

  nor nor_1 (nor_1_out, I_100, I_101, J_111);
  or or_1 (or_1_out, R_000, I_011, I_100, I_110);
  nor nor_2 (MUX_ula_op, R_000, R_001, R_010);
  nor nor_3 (MUX_r1_select, R_000, R_001, R_010);
  nor nor_4 (MUX_r2_select, R_000, R_001, R_010);
  or or_2 (MUX_r_data_select, I_011, I_110);
  or or_3 (MUX_ula_b, I_011, I_100, I_110);
  or or_4 (or_4_out, R_000, I_100, I_101, I_110, J_111);
  not not_1 (DMX_r2_out, R_000);
  PORT_AND port_and_1 (
    .in_1(1'b1), .in_2(1'b1), .in_3(nor_1_out), .in_4(or_1_out), .in_5(or_1_out), .COMUM(on_off),
    .out_1(pc_en), .out_2(r_en), .out_3(REG_EN_WRITE), .out_4(REG_ULA_EN), .out_5(alu_en));  // open: in_6, in_7, in_8, in_9, in_10, in_11, in_12, in_13, in_14, out_6, out_7, out_8, out_9, out_10, out_11, out_12, out_13, out_14
  assign MUX_reg_data = or_4_out ? 2'b00 : 2'bz;  // Controlled_Buffer controlled_buffer_1
  assign MUX_R = R_000 ? 2'b00 : 2'bz;  // Controlled_Buffer controlled_buffer_2
  assign MUX_I = I_011 ? 2'b00 : 2'bz;  // Controlled_Buffer controlled_buffer_3
  assign MUX_reg_data = R_001 ? 2'b01 : 2'bz;  // Controlled_Buffer controlled_buffer_4
  assign MUX_reg_data = R_010 ? 2'b10 : 2'bz;  // Controlled_Buffer controlled_buffer_5
  assign MUX_R = R_001 ? 2'b01 : 2'bz;  // Controlled_Buffer controlled_buffer_6
  assign MUX_R = R_010 ? 2'b10 : 2'bz;  // Controlled_Buffer controlled_buffer_7
  assign MUX_I = I_100 ? 2'b01 : 2'bz;  // Controlled_Buffer controlled_buffer_8
  assign MUX_I = I_101 ? 2'b10 : 2'bz;  // Controlled_Buffer controlled_buffer_9
  assign MUX_reg_data = I_011 ? 2'b11 : 2'bz;  // Controlled_Buffer controlled_buffer_10
  assign MUX_I = I_110 ? 2'b11 : 2'bz;  // Controlled_Buffer controlled_buffer_11
  Multiplexer #(.width(3)) multiplexer_1 (.in0(RS_R), .in1(RS_I), .out(r1_select), .sel(MUX_r1_select), .en(1'b1));
  Multiplexer #(.width(3)) multiplexer_2 (.in0(RT_R), .in1(RT_I), .out(r2_select), .sel(MUX_r2_select), .en(1'b1));
  PORT_AND port_and_2 (
    .in_1(1'b1), .in_2(1'b1), .in_3(1'b1), .in_4(1'b1), .in_5(1'b1), .in_6(1'b1), .in_7(1'b1), .in_8(1'b1),
    .in_9(1'b1), .in_10(1'b1), .in_11(1'b1), .in_12(1'b1), .in_13(1'b1), .in_14(1'b1), .COMUM(Reset),
    .out_1(pc_cl), .out_2(r_cl), .out_3(regs_cl), .out_4(mem_cl));  // open: out_5, out_6, out_7, out_8, out_9, out_10, out_11, out_12, out_13, out_14
  Multiplexer #(.width(3)) multiplexer_3 (
    .in0(RD_R), .in1(RT_I), .out(r_data_select), .sel(MUX_r_data_select), .en(1'b1));
  Multiplexer #(.select(2), .width(8)) multiplexer_4 (
    .in0(A_B), .in1(RESULT_SHIFT), .in2(RESULT_LESS), .in3(load_mem_data), .out(REG_DATA),
    .sel(MUX_reg_data), .en(1'b1));
  Demultiplexer #(.select(3), .width(16)) demultiplexer_1 (
    .out0(demultiplexer_1_out0), .out1(demultiplexer_1_out1), .out2(demultiplexer_1_out2),
    .out3(demultiplexer_1_out3), .out4(demultiplexer_1_out4), .out5(demultiplexer_1_out5),
    .out6(demultiplexer_1_out6), .out7(demultiplexer_1_out7), .in(data_instr), .sel(data_instr[15:13]),
    .en(1'b1));
  Decoder #(.select(3), .enable("false")) decoder_1 (
    .out0(R_000), .out1(R_001), .out2(R_010), .out3(I_011), .out4(I_100), .out5(I_101), .out6(I_110),
    .out7(J_111), .sel(data_instr[15:13]));
  Multiplexer #(.select(2), .width(16)) multiplexer_5 (
    .in0(demultiplexer_1_out0), .in1(demultiplexer_1_out1), .in2(demultiplexer_1_out2),
    .out({multiplexer_5_out, RS_R, RT_R, RD_R, SHIFT_R, FUNC_R}), .sel(MUX_R), .en(1'b1));  // open: in3
  Multiplexer #(.select(2), .width(16)) multiplexer_6 (
    .in0(demultiplexer_1_out3), .in1(demultiplexer_1_out4), .in2(demultiplexer_1_out5),
    .in3(demultiplexer_1_out6), .out({multiplexer_6_out[15:13], RS_I, RT_I, multiplexer_6_out[6:0]}),
    .sel(MUX_I), .en(1'b1));
  Demultiplexer #(.width(8)) demultiplexer_2 (
    .out0(R2_OUT_B), .out1(write_mem_data), .in(r2_out), .sel(DMX_r2_out), .en(1'b1));
  assign mem_data_adrress = and_1_out ? {8{1'b0}} : 8'bz;  // Controlled_Buffer controlled_buffer_12
  and and_1 (and_1_out, not_2_out, not_3_out);
  Bit_Extender #(.in_width(13), .out_width(4)) bit_extender_1 (.in(demultiplexer_1_out7[12:0]), .out(ADDR_J));
  not not_2 (not_2_out, and_2_out);
  assign IMM_I = {{1{1'b0}}, multiplexer_6_out[6:0]};  // Bit_Extender bit_extender_2
  assign mem_data_adrress = and_2_out ? A_B : 8'bz;  // Controlled_Buffer controlled_buffer_13
  not not_3 (not_3_out, I_100);
  and and_2 (and_2_out, not_3_out, I_011);
  assign mem_data_adrress = I_100 ? alu_out : 8'bz;  // Controlled_Buffer controlled_buffer_14
  not not_4 (mem_s_r, I_100);
  Multiplexer #(.width(8)) multiplexer_7 (.in0(R2_OUT_B), .in1(IMM_I), .out(alu_b), .sel(MUX_ula_b), .en(1'b1));
  Multiplexer #(.width(3)) multiplexer_8 (.in0(FUNC_R), .in1(3'b000), .out(alu_op), .sel(MUX_ula_op), .en(1'b1));
  Comparator comparator_1 (.a(r1_out), .b(write_mem_data), .eq(comparator_1_eq));  // open: gt, lt
  Shifter shifter_1 (.in(write_mem_data), .\dist (RS_R), .out(RESULT_SHIFT));
  Comparator comparator_2 (.a(r1_out), .b(write_mem_data), .lt(comparator_2_lt));  // open: gt, eq
  Bit_Extender #(.out_width(4)) bit_extender_3 (.in(IMM_I), .out(bit_extender_3_out));
  assign pc_in = and_3_out ? bit_extender_3_out : 4'bz;  // Controlled_Buffer controlled_buffer_15
  and and_3 (and_3_out, comparator_1_eq, I_101);
  Multiplexer #(.width(8)) multiplexer_9 (
    .in0({8{1'b0}}), .in1(8'h1), .out(RESULT_LESS), .sel(comparator_2_lt), .en(1'b1));
  Register register_1 (.D(alu_out), .en(REG_ULA_EN), .Q(A_B), .clk(CLOCK));  // open: clr
  not not_5 (cpi_en, adder_1_cout);
  assign pc_in = nor_5_out ? adder_1_out : 4'bz;  // Controlled_Buffer controlled_buffer_16
  Adder #(.width(4)) adder_1 (.a(pc_out), .b(4'b0001), .out(adder_1_out), .cout(adder_1_cout));  // open: cin
  nor nor_5 (nor_5_out, and_3_out, J_111);
  assign pc_in = J_111 ? ADDR_J : 4'bz;  // Controlled_Buffer controlled_buffer_17

  assign alu_a = r1_out;

  // Other names for the same wires on the sheet: LOAD[7:0] = load_mem_data; R2_OUT_t[7:0] = write_mem_data;
  //   REG_EN_W = REG_EN_WRITE; RI_CL = r_cl; RI_EN = r_en; RS_IMM[7:0] = alu_out; ULA_EN = alu_en
endmodule

module ALU (
  input  [7:0] IN_A,
  input  [7:0] IN_B,
  input  [2:0] Select,
  input  Enable,
  output [7:0] OUT
);

  wire [7:0] adder_1_out, and_1_out, divider_1_out, multiplier_1_out, not_1_out, or_1_out, subtractor_1_out,
       undriven;

  Adder adder_1 (.a(IN_A), .b(IN_B), .out(adder_1_out));  // open: cin, cout
  Subtractor subtractor_1 (.a(IN_A), .b(IN_B), .out(subtractor_1_out));  // open: bin, bout
  Multiplier multiplier_1 (.a(IN_A), .b(IN_B), .out(multiplier_1_out));  // open: cin, cout
  Divider divider_1 (.a(IN_A), .b(IN_B), .out(divider_1_out));  // open: upper, rem
  assign and_1_out = IN_A & IN_B;  // AND_Gate and_1, 8 bits wide
  assign or_1_out = IN_A | IN_B;  // OR_Gate or_1, 8 bits wide
  assign not_1_out = ~IN_A;  // NOT_Gate not_1, 8 bits wide
  Multiplexer #(.select(3), .width(8)) multiplexer_1 (
    .in0(adder_1_out), .in1(subtractor_1_out), .in2(multiplier_1_out), .in3(divider_1_out), .in4(and_1_out),
    .in5(or_1_out), .in6(not_1_out), .in7(undriven), .out(OUT), .sel(Select), .en(Enable));
endmodule

// REGITERS
module REGISTERS (
  input  [7:0] DATA,
  input  CLOCK,
  input  CLEAR,
  input  [2:0] SELECT_OUT_1,
  input  [2:0] SELECT_OUT_2,
  input  ENABLE,
  input  [2:0] SELECT_WRITE,
  output [7:0] OUT_1,
  output [7:0] OUT_2
);

  wire demultiplexer_2_out0, demultiplexer_2_out1, demultiplexer_2_out2, demultiplexer_2_out3,
       demultiplexer_2_out4, demultiplexer_2_out5, demultiplexer_2_out6, demultiplexer_2_out7;
  wire [7:0] demultiplexer_1_out1, demultiplexer_1_out2, demultiplexer_1_out3, demultiplexer_1_out4,
       demultiplexer_1_out5, demultiplexer_1_out6, demultiplexer_1_out7, register_1_q, register_2_q,
       register_3_q, register_4_q, register_5_q, register_6_q, register_7_q, register_8_q;

  Demultiplexer #(.select(3), .width(8)) demultiplexer_1 (
    .out1(demultiplexer_1_out1), .out2(demultiplexer_1_out2), .out3(demultiplexer_1_out3),
    .out4(demultiplexer_1_out4), .out5(demultiplexer_1_out5), .out6(demultiplexer_1_out6),
    .out7(demultiplexer_1_out7), .in(DATA), .sel(SELECT_WRITE), .en(1'b1));  // open: out0
  Demultiplexer #(.select(3)) demultiplexer_2 (
    .out0(demultiplexer_2_out0), .out1(demultiplexer_2_out1), .out2(demultiplexer_2_out2),
    .out3(demultiplexer_2_out3), .out4(demultiplexer_2_out4), .out5(demultiplexer_2_out5),
    .out6(demultiplexer_2_out6), .out7(demultiplexer_2_out7), .in(ENABLE), .sel(SELECT_WRITE), .en(1'b1));
  Register register_1 (.D(demultiplexer_1_out7), .en(demultiplexer_2_out7), .Q(register_1_q), .clk(CLOCK), .clr(CLEAR));
  Register register_2 (.D(demultiplexer_1_out6), .en(demultiplexer_2_out6), .Q(register_2_q), .clk(CLOCK), .clr(CLEAR));
  Register register_3 (.D(demultiplexer_1_out5), .en(demultiplexer_2_out5), .Q(register_3_q), .clk(CLOCK), .clr(CLEAR));
  Register register_4 (.D(demultiplexer_1_out4), .en(demultiplexer_2_out4), .Q(register_4_q), .clk(CLOCK), .clr(CLEAR));
  Register register_5 (.D(demultiplexer_1_out3), .en(demultiplexer_2_out3), .Q(register_5_q), .clk(CLOCK), .clr(CLEAR));
  Register register_6 (.D(demultiplexer_1_out2), .en(demultiplexer_2_out2), .Q(register_6_q), .clk(CLOCK), .clr(CLEAR));
  Register register_7 (.D(demultiplexer_1_out1), .en(demultiplexer_2_out1), .Q(register_7_q), .clk(CLOCK), .clr(CLEAR));
  Register register_8 (.D({8{1'b0}}), .en(demultiplexer_2_out0), .Q(register_8_q), .clk(CLOCK), .clr(CLEAR));
  Multiplexer #(.select(3), .width(8)) multiplexer_1 (
    .in0(register_8_q), .in1(register_7_q), .in2(register_6_q), .in3(register_5_q), .in4(register_4_q),
    .in5(register_3_q), .in6(register_2_q), .in7(register_1_q), .out(OUT_1), .sel(SELECT_OUT_1), .en(1'b1));
  Multiplexer #(.select(3), .width(8)) multiplexer_2 (
    .in0(register_8_q), .in1(register_7_q), .in2(register_6_q), .in3(register_5_q), .in4(register_4_q),
    .in5(register_3_q), .in6(register_2_q), .in7(register_1_q), .out(OUT_2), .sel(SELECT_OUT_2), .en(1'b1));
endmodule

module SHOW_INSTR (
  input  [15:0] Input,
  output [3:0] mais_sign,
  output [3:0] out_3,
  output [3:0] out_4,
  output [3:0] out_5,
  output [3:0] out_6,
  output [3:0] out_7,
  output [3:0] out_8,
  output [3:0] out_9,
  output [3:0] out_10,
  output [3:0] out_11,
  output [3:0] out_12,
  output [3:0] out_13,
  output [3:0] out_14,
  output [3:0] out_15,
  output [3:0] out_16,
  output [3:0] menos_sign
);

  assign menos_sign = {{3{1'b0}}, Input[0]};  // Bit_Extender bit_extender_1
  assign out_16 = {{3{1'b0}}, Input[1]};  // Bit_Extender bit_extender_2
  assign out_15 = {{3{1'b0}}, Input[2]};  // Bit_Extender bit_extender_3
  assign out_14 = {{3{1'b0}}, Input[3]};  // Bit_Extender bit_extender_4
  assign out_13 = {{3{1'b0}}, Input[4]};  // Bit_Extender bit_extender_5
  assign out_12 = {{3{1'b0}}, Input[5]};  // Bit_Extender bit_extender_6
  assign out_11 = {{3{1'b0}}, Input[6]};  // Bit_Extender bit_extender_7
  assign out_10 = {{3{1'b0}}, Input[7]};  // Bit_Extender bit_extender_8
  assign out_9 = {{3{1'b0}}, Input[8]};  // Bit_Extender bit_extender_9
  assign out_8 = {{3{1'b0}}, Input[9]};  // Bit_Extender bit_extender_10
  assign out_7 = {{3{1'b0}}, Input[10]};  // Bit_Extender bit_extender_11
  assign out_6 = {{3{1'b0}}, Input[11]};  // Bit_Extender bit_extender_12
  assign out_5 = {{3{1'b0}}, Input[12]};  // Bit_Extender bit_extender_13
  assign out_4 = {{3{1'b0}}, Input[13]};  // Bit_Extender bit_extender_14
  assign out_3 = {{3{1'b0}}, Input[14]};  // Bit_Extender bit_extender_15
  assign mais_sign = {{3{1'b0}}, Input[15]};  // Bit_Extender bit_extender_16
endmodule

// AND
module PORT_AND (
  input  COMUM,
  input  in_1,
  input  in_2,
  input  in_3,
  input  in_4,
  input  in_5,
  input  in_6,
  input  in_7,
  input  in_8,
  input  in_9,
  input  in_10,
  input  in_11,
  input  in_12,
  input  in_13,
  input  in_14,
  output out_1,
  output out_2,
  output out_3,
  output out_4,
  output out_5,
  output out_6,
  output out_7,
  output out_8,
  output out_9,
  output out_10,
  output out_11,
  output out_12,
  output out_13,
  output out_14
);

  and and_1 (out_1, COMUM, in_1);
  and and_2 (out_2, COMUM, in_2);
  and and_3 (out_3, COMUM, in_3);
  and and_4 (out_4, COMUM, in_4);
  and and_5 (out_5, COMUM, in_5);
  and and_6 (out_6, COMUM, in_6);
  and and_7 (out_7, COMUM, in_7);
  and and_8 (out_8, COMUM, in_8);
  and and_9 (out_9, COMUM, in_9);
  and and_10 (out_10, COMUM, in_10);
  and and_11 (out_11, COMUM, in_11);
  and and_12 (out_12, COMUM, in_12);
  and and_13 (out_13, COMUM, in_13);
  and and_14 (out_14, COMUM, in_14);
endmodule

module CPU (
  input  CLOCK,
  input  ON_OFF,
  input  RESET,
  output [15:0] INSTRUCTION,
  output READ_MEM,
  output WRITE_MEM,
  output [7:0] S0,
  output [7:0] S1,
  output [7:0] S2,
  output [7:0] T0,
  output [7:0] T1,
  output [7:0] D0,
  output [7:0] D1
);

  wire controller_1_alu_en, controller_1_cpi_en, controller_1_mem_cl, controller_1_pc_cl, controller_1_pc_en,
       controller_1_r_cl, controller_1_r_en, controller_1_reg_en_write, controller_1_regs_cl,
       count_cpi_1_pulso, not_1_out;
  wire [2:0] controller_1_alu_op, controller_1_r1_select, controller_1_r2_select, controller_1_r_data_select;
  wire [3:0] controller_1_pc_in, PC_q, show_instr_1_mais_sign, show_instr_1_menos_sign, show_instr_1_out_3,
       show_instr_1_out_4, show_instr_1_out_5, show_instr_1_out_6, show_instr_1_out_7, show_instr_1_out_8,
       show_instr_1_out_9, show_instr_1_out_10, show_instr_1_out_11, show_instr_1_out_12,
       show_instr_1_out_13, show_instr_1_out_14, show_instr_1_out_15, show_instr_1_out_16;
  wire [6:0] bit_extender_1_out;
  wire [7:0] alu_1_out, controlled_buffer_2_out, controller_1_alu_a, controller_1_alu_b,
       controller_1_mem_data_adrress, controller_1_reg_data, controller_1_write_mem_data, ram_1_data,
       regiters_show_1_out_1, regiters_show_1_out_2;
  wire [15:0] rom_1_data;

  COUNT_CPI count_cpi_1 (.PULSO(count_cpi_1_pulso), .Enable(controller_1_cpi_en), .Clock(CLOCK));  // open: Clear
  CONTROLLER controller_1 (
    .pc_en(controller_1_pc_en), .pc_cl(controller_1_pc_cl), .r_en(controller_1_r_en),
    .r_cl(controller_1_r_cl), .data_instr(INSTRUCTION), .mem_data_adrress(controller_1_mem_data_adrress),
    .mem_s_r(READ_MEM), .mem_cl(controller_1_mem_cl), .load_mem_data(controlled_buffer_2_out),
    .on_off(ON_OFF), .Reset(RESET), .r1_select(controller_1_r1_select), .r2_select(controller_1_r2_select),
    .r_data_select(controller_1_r_data_select), .REG_DATA(controller_1_reg_data),
    .regs_cl(controller_1_regs_cl), .r1_out(regiters_show_1_out_1), .r2_out(regiters_show_1_out_2),
    .alu_a(controller_1_alu_a), .alu_b(controller_1_alu_b), .alu_op(controller_1_alu_op),
    .alu_en(controller_1_alu_en), .alu_out(alu_1_out), .pc_out(PC_q), .pc_in(controller_1_pc_in),
    .REG_EN_WRITE(controller_1_reg_en_write), .CLOCK(CLOCK), .cpi_en(controller_1_cpi_en),
    .write_mem_data(controller_1_write_mem_data));
  Hex_Digit_Display hex_digit_display_1 (.value(show_instr_1_mais_sign));  // open: dp
  Hex_Digit_Display hex_digit_display_2 (.value(show_instr_1_out_3));  // open: dp
  SHOW_INSTR show_instr_1 (
    .Input(INSTRUCTION), .mais_sign(show_instr_1_mais_sign), .out_3(show_instr_1_out_3),
    .out_4(show_instr_1_out_4), .out_5(show_instr_1_out_5), .out_6(show_instr_1_out_6),
    .out_7(show_instr_1_out_7), .out_8(show_instr_1_out_8), .out_9(show_instr_1_out_9),
    .out_10(show_instr_1_out_10), .out_11(show_instr_1_out_11), .out_12(show_instr_1_out_12),
    .out_13(show_instr_1_out_13), .out_14(show_instr_1_out_14), .out_15(show_instr_1_out_15),
    .out_16(show_instr_1_out_16), .menos_sign(show_instr_1_menos_sign));
  Register #(.width(4)) PC (
    .D(controller_1_pc_in), .en(controller_1_pc_en), .Q(PC_q), .clk(count_cpi_1_pulso),
    .clr(controller_1_pc_cl));
  Hex_Digit_Display hex_digit_display_3 (.value(show_instr_1_out_4));  // open: dp
  REGITERS_SHOW regiters_show_1 (
    .DATA(controller_1_reg_data), .SELECT_WRITE(controller_1_r_data_select), .OUT_1(regiters_show_1_out_1),
    .SELECT_OUT_1(controller_1_r1_select), .OUT_2(regiters_show_1_out_2),
    .SELECT_OUT_2(controller_1_r2_select), .CLOCK(CLOCK), .ENABLE(controller_1_reg_en_write),
    .CLEAR(controller_1_regs_cl), .D1(D1), .D0(D0), .T1(T1), .T0(T0), .S2(S2), .S1(S1), .S0(S0));
  Hex_Digit_Display hex_digit_display_4 (.value(show_instr_1_out_6));  // open: dp
  Hex_Digit_Display hex_digit_display_5 (.value(show_instr_1_out_5));  // open: dp
  ROM #(.addrWidth(4), .dataWidth(16)) rom_1 (.addr(PC_q), .data(rom_1_data));  // open: sel
  Register #(.width(16)) register_1 (
    .D(rom_1_data), .en(controller_1_r_en), .Q(INSTRUCTION), .clk(CLOCK), .clr(controller_1_r_cl));
  Hex_Digit_Display hex_digit_display_6 (.value(show_instr_1_out_8));  // open: dp
  Hex_Digit_Display hex_digit_display_7 (.value(show_instr_1_out_7));  // open: dp
  Hex_Digit_Display hex_digit_display_8 (.value(show_instr_1_out_10));  // open: dp
  Hex_Digit_Display hex_digit_display_9 (.value(show_instr_1_out_9));  // open: dp
  Hex_Digit_Display hex_digit_display_10 (.value(show_instr_1_out_12));  // open: dp
  Hex_Digit_Display hex_digit_display_11 (.value(show_instr_1_out_11));  // open: dp
  Bit_Extender #(.out_width(7)) bit_extender_1 (.in(controller_1_mem_data_adrress), .out(bit_extender_1_out));
  ALU alu_1 (
    .IN_A(controller_1_alu_a), .IN_B(controller_1_alu_b), .OUT(alu_1_out), .Select(controller_1_alu_op),
    .Enable(controller_1_alu_en));
  Hex_Digit_Display hex_digit_display_12 (.value(show_instr_1_out_14));  // open: dp
  Hex_Digit_Display hex_digit_display_13 (.value(show_instr_1_out_13));  // open: dp
  Hex_Digit_Display hex_digit_display_14 (.value(show_instr_1_out_16));  // open: dp
  Hex_Digit_Display hex_digit_display_15 (.value(show_instr_1_out_15));  // open: dp
  RAM #(.addrWidth(7)) ram_1 (
    .addr(bit_extender_1_out), .data(ram_1_data), .clk(CLOCK), .ld(READ_MEM), .clr(controller_1_mem_cl));  // open: sel
  assign ram_1_data = not_1_out ? controller_1_write_mem_data : 8'bz;  // Controlled_Buffer controlled_buffer_1
  not not_1 (not_1_out, READ_MEM);
  Hex_Digit_Display hex_digit_display_16 (.value(show_instr_1_menos_sign));  // open: dp
  assign controlled_buffer_2_out = READ_MEM ? ram_1_data : 8'bz;  // Controlled_Buffer controlled_buffer_2
  not not_2 (WRITE_MEM, READ_MEM);

  // Other names for the same wires on the sheet: INSTR[15:0] = INSTRUCTION

  // Notes on the sheet:
  //   contents of rom_1 (hex, n*v repeats v):
  //   c080 c101 c182 150 49e7 4af7 374f 2a1f e008
endmodule

module LEDS (
  input  in_1,
  input  in_2,
  input  ON_OFF,
  input  in_4,
  input  in_5,
  input  [6:0] in_6,
  input  [6:0] in_7,
  input  [6:0] in_8,
  output [6:0] out_9,
  output out_10
);

  wire clock_2_out, clock_out, controller_1_alu_en, controller_1_cpi_en, controller_1_mem_cl,
       controller_1_mem_s_r, controller_1_pc_cl, controller_1_pc_en, controller_1_r_cl, controller_1_r_en,
       controller_1_reg_en_write, controller_1_regs_cl, count_cpi_1_pulso, not_1_out, RESET_out;
  wire [2:0] controller_1_alu_op, controller_1_r1_select, controller_1_r2_select, controller_1_r_data_select;
  wire [3:0] controller_1_pc_in, PC_q, show_instr_1_mais_sign, show_instr_1_menos_sign, show_instr_1_out_3,
       show_instr_1_out_4, show_instr_1_out_5, show_instr_1_out_6, show_instr_1_out_7, show_instr_1_out_8,
       show_instr_1_out_9, show_instr_1_out_10, show_instr_1_out_11, show_instr_1_out_12,
       show_instr_1_out_13, show_instr_1_out_14, show_instr_1_out_15, show_instr_1_out_16;
  wire [6:0] bit_extender_1_out, keyboard_2_data;
  wire [7:0] alu_1_out, controller_1_alu_a, controller_1_alu_b, controller_1_mem_data_adrress,
       controller_1_reg_data, ram_1_data, registers_1_out_1, registers_1_out_2;
  wire [15:0] INSTR, rom_1_data;

  Button RESET (.out(RESET_out));
  COUNT_CPI count_cpi_1 (.PULSO(count_cpi_1_pulso), .Enable(controller_1_cpi_en), .Clock(clock_out));  // open: Clear
  CONTROLLER controller_1 (
    .pc_en(controller_1_pc_en), .pc_cl(controller_1_pc_cl), .r_en(controller_1_r_en),
    .r_cl(controller_1_r_cl), .data_instr(INSTR), .mem_data_adrress(controller_1_mem_data_adrress),
    .mem_s_r(controller_1_mem_s_r), .mem_cl(controller_1_mem_cl), .on_off(ON_OFF), .Reset(RESET_out),
    .r1_select(controller_1_r1_select), .r2_select(controller_1_r2_select),
    .r_data_select(controller_1_r_data_select), .REG_DATA(controller_1_reg_data),
    .regs_cl(controller_1_regs_cl), .r1_out(registers_1_out_1), .r2_out(registers_1_out_2),
    .alu_a(controller_1_alu_a), .alu_b(controller_1_alu_b), .alu_op(controller_1_alu_op),
    .alu_en(controller_1_alu_en), .alu_out(alu_1_out), .pc_out(PC_q), .pc_in(controller_1_pc_in),
    .REG_EN_WRITE(controller_1_reg_en_write), .CLOCK(clock_out), .cpi_en(controller_1_cpi_en));  // open: load_mem_data, write_mem_data
  Hex_Digit_Display hex_digit_display_1 (.value(show_instr_1_mais_sign));  // open: dp
  Hex_Digit_Display hex_digit_display_2 (.value(show_instr_1_out_3));  // open: dp
  SHOW_INSTR show_instr_1 (
    .Input(INSTR), .mais_sign(show_instr_1_mais_sign), .out_3(show_instr_1_out_3),
    .out_4(show_instr_1_out_4), .out_5(show_instr_1_out_5), .out_6(show_instr_1_out_6),
    .out_7(show_instr_1_out_7), .out_8(show_instr_1_out_8), .out_9(show_instr_1_out_9),
    .out_10(show_instr_1_out_10), .out_11(show_instr_1_out_11), .out_12(show_instr_1_out_12),
    .out_13(show_instr_1_out_13), .out_14(show_instr_1_out_14), .out_15(show_instr_1_out_15),
    .out_16(show_instr_1_out_16), .menos_sign(show_instr_1_menos_sign));
  Register #(.width(4)) PC (
    .D(controller_1_pc_in), .en(controller_1_pc_en), .Q(PC_q), .clk(count_cpi_1_pulso),
    .clr(controller_1_pc_cl));
  REGISTERS registers_1 (
    .DATA(controller_1_reg_data), .SELECT_WRITE(controller_1_r_data_select), .OUT_1(registers_1_out_1),
    .ENABLE(controller_1_reg_en_write), .CLOCK(clock_out), .CLEAR(controller_1_regs_cl),
    .OUT_2(registers_1_out_2), .SELECT_OUT_2(controller_1_r2_select), .SELECT_OUT_1(controller_1_r1_select));
  Hex_Digit_Display hex_digit_display_3 (.value(show_instr_1_out_4));  // open: dp
  Hex_Digit_Display hex_digit_display_4 (.value(show_instr_1_out_6));  // open: dp
  Hex_Digit_Display hex_digit_display_5 (.value(show_instr_1_out_5));  // open: dp
  ROM #(.addrWidth(4), .dataWidth(16)) rom_1 (.addr(PC_q), .data(rom_1_data));  // open: sel
  Register #(.width(16)) register_1 (
    .D(rom_1_data), .en(controller_1_r_en), .Q(INSTR), .clk(clock_out), .clr(controller_1_r_cl));
  Hex_Digit_Display hex_digit_display_6 (.value(show_instr_1_out_8));  // open: dp
  Hex_Digit_Display hex_digit_display_7 (.value(show_instr_1_out_7));  // open: dp
  Hex_Digit_Display hex_digit_display_8 (.value(show_instr_1_out_9));  // open: dp
  Hex_Digit_Display hex_digit_display_9 (.value(show_instr_1_out_10));  // open: dp
  Hex_Digit_Display hex_digit_display_10 (.value(show_instr_1_out_11));  // open: dp
  Hex_Digit_Display hex_digit_display_11 (.value(show_instr_1_out_12));  // open: dp
  Bit_Extender #(.out_width(7)) bit_extender_1 (.in(controller_1_mem_data_adrress), .out(bit_extender_1_out));
  ALU alu_1 (
    .IN_A(controller_1_alu_a), .IN_B(controller_1_alu_b), .OUT(alu_1_out), .Select(controller_1_alu_op),
    .Enable(controller_1_alu_en));
  Hex_Digit_Display hex_digit_display_12 (.value(show_instr_1_out_14));  // open: dp
  Hex_Digit_Display hex_digit_display_13 (.value(show_instr_1_out_13));  // open: dp
  Hex_Digit_Display hex_digit_display_14 (.value(show_instr_1_out_16));  // open: dp
  Hex_Digit_Display hex_digit_display_15 (.value(show_instr_1_out_15));  // open: dp
  RAM #(.addrWidth(7)) ram_1 (
    .addr(bit_extender_1_out), .data(ram_1_data), .clk(clock_out), .ld(controller_1_mem_s_r),
    .clr(controller_1_mem_cl));  // open: sel
  Hex_Digit_Display hex_digit_display_16 (.value(show_instr_1_menos_sign));  // open: dp
  LED WRITE (.in(not_1_out));
  LED READ (.in(controller_1_mem_s_r));
  not not_1 (not_1_out, controller_1_mem_s_r);
  Clock clock (.out(clock_out));
  Keyboard keyboard_1 (.clk(clock_2_out), .re(clock_2_out), .clr(in_1), .data(out_9));  // open: avail
  Clock clock_2 (.out(clock_2_out));
  DotMatrix dotmatrix_1 (.col0(in_6), .col1(in_7), .col2(in_8));  // open: col3, col4
  TTY tty_1 (.data(keyboard_2_data), .clk(clock_2_out), .we(in_4), .clr(in_2));
  Keyboard keyboard_2 (.clk(clock_2_out), .re(clock_2_out), .clr(in_5), .avail(out_10), .data(keyboard_2_data));

  // Notes on the sheet:
  //   contents of rom_1 (hex, n*v repeats v):
  //   c081 c102 c183 c204 c285 c306 c387 e007
endmodule

// CPI
module COUNT_CPI (
  input  Enable,
  input  Clear,
  input  Clock,
  output PULSO
);

  wire [1:0] adder_1_out, register_1_q;

  Adder #(.width(2)) adder_1 (.a(register_1_q), .b(2'b01), .out(adder_1_out), .cout(PULSO));  // open: cin
  Register #(.width(2)) register_1 (.D(adder_1_out), .en(Enable), .Q(register_1_q), .clk(Clock), .clr(Clear));
endmodule

// RESGISTERS
module REGITERS_SHOW (
  input  [7:0] DATA,
  input  CLOCK,
  input  CLEAR,
  input  [2:0] SELECT_OUT_1,
  input  [2:0] SELECT_OUT_2,
  input  ENABLE,
  input  [2:0] SELECT_WRITE,
  output [7:0] D1,
  output [7:0] D0,
  output [7:0] T1,
  output [7:0] T0,
  output [7:0] S2,
  output [7:0] S1,
  output [7:0] S0,
  output [7:0] OUT_1,
  output [7:0] OUT_2
);

  wire demultiplexer_2_out0, demultiplexer_2_out1, demultiplexer_2_out2, demultiplexer_2_out3,
       demultiplexer_2_out4, demultiplexer_2_out5, demultiplexer_2_out6, demultiplexer_2_out7;
  wire [7:0] demultiplexer_1_out1, demultiplexer_1_out2, demultiplexer_1_out3, demultiplexer_1_out4,
       demultiplexer_1_out5, demultiplexer_1_out6, demultiplexer_1_out7, register_8_q;

  Demultiplexer #(.select(3), .width(8)) demultiplexer_1 (
    .out1(demultiplexer_1_out1), .out2(demultiplexer_1_out2), .out3(demultiplexer_1_out3),
    .out4(demultiplexer_1_out4), .out5(demultiplexer_1_out5), .out6(demultiplexer_1_out6),
    .out7(demultiplexer_1_out7), .in(DATA), .sel(SELECT_WRITE), .en(1'b1));  // open: out0
  Demultiplexer #(.select(3)) demultiplexer_2 (
    .out0(demultiplexer_2_out0), .out1(demultiplexer_2_out1), .out2(demultiplexer_2_out2),
    .out3(demultiplexer_2_out3), .out4(demultiplexer_2_out4), .out5(demultiplexer_2_out5),
    .out6(demultiplexer_2_out6), .out7(demultiplexer_2_out7), .in(ENABLE), .sel(SELECT_WRITE), .en(1'b1));
  Register register_1 (.D(demultiplexer_1_out7), .en(demultiplexer_2_out7), .Q(D1), .clk(CLOCK), .clr(CLEAR));
  Register register_2 (.D(demultiplexer_1_out6), .en(demultiplexer_2_out6), .Q(D0), .clk(CLOCK), .clr(CLEAR));
  Register register_3 (.D(demultiplexer_1_out5), .en(demultiplexer_2_out5), .Q(T1), .clk(CLOCK), .clr(CLEAR));
  Register register_4 (.D(demultiplexer_1_out4), .en(demultiplexer_2_out4), .Q(T0), .clk(CLOCK), .clr(CLEAR));
  Register register_5 (.D(demultiplexer_1_out3), .en(demultiplexer_2_out3), .Q(S2), .clk(CLOCK), .clr(CLEAR));
  Register register_6 (.D(demultiplexer_1_out2), .en(demultiplexer_2_out2), .Q(S1), .clk(CLOCK), .clr(CLEAR));
  Register register_7 (.D(demultiplexer_1_out1), .en(demultiplexer_2_out1), .Q(S0), .clk(CLOCK), .clr(CLEAR));
  Register register_8 (.D({8{1'b0}}), .en(demultiplexer_2_out0), .Q(register_8_q), .clk(CLOCK), .clr(CLEAR));
  Multiplexer #(.select(3), .width(8)) multiplexer_1 (
    .in0(register_8_q), .in1(S0), .in2(S1), .in3(S2), .in4(T0), .in5(T1), .in6(D0), .in7(D1), .out(OUT_1),
    .sel(SELECT_OUT_1), .en(1'b1));
  Multiplexer #(.select(3), .width(8)) multiplexer_2 (
    .in0(register_8_q), .in1(S0), .in2(S1), .in3(S2), .in4(T0), .in5(T1), .in6(D0), .in7(D1), .out(OUT_2),
    .sel(SELECT_OUT_2), .en(1'b1));
endmodule

module SHOW (
  input  [7:0] IN,
  output A1,
  output A0,
  output A6,
  output A5,
  output A4,
  output A2,
  output A3,
  output B1,
  output B0,
  output B6,
  output B5,
  output B4,
  output B2,
  output B3,
  output C1,
  output C0,
  output C6,
  output C5,
  output C4,
  output C2,
  output C3
);

  wire bcd_aux_1_a3, bcd_aux_1_a4, bcd_aux_1_b1, bcd_aux_1_b2, bcd_aux_1_b3, bcd_aux_1_b4, bcd_aux_1_c1,
       bcd_aux_1_c2, bcd_aux_1_c3, bcd_aux_1_c4;

  BCD_AUX bcd_aux_1 (
    .A(IN[7]), .B(IN[6]), .C(IN[5]), .D(IN[4]), .E(IN[3]), .F(IN[2]), .G(IN[1]), .H(IN[0]),
    .A3(bcd_aux_1_a3), .A4(bcd_aux_1_a4), .B1(bcd_aux_1_b1), .B2(bcd_aux_1_b2), .B3(bcd_aux_1_b3),
    .B4(bcd_aux_1_b4), .C1(bcd_aux_1_c1), .C2(bcd_aux_1_c2), .C3(bcd_aux_1_c3), .C4(bcd_aux_1_c4));
  BCD_7_SEG bcd_7_seg_1 (
    .D(bcd_aux_1_c1), .C(bcd_aux_1_c2), .B(bcd_aux_1_c3), .A(bcd_aux_1_c4), .a_2(C1), .b_2(C0), .c_2(C6),
    .d_2(C5), .e(C4), .f(C2), .g(C3));
  BCD_7_SEG bcd_7_seg_2 (
    .D(1'b0), .C(1'b0), .B(bcd_aux_1_a3), .A(bcd_aux_1_a4), .a_2(A1), .b_2(A0), .c_2(A6), .d_2(A5), .e(A4),
    .f(A2), .g(A3));
  BCD_7_SEG bcd_7_seg_3 (
    .D(bcd_aux_1_b1), .C(bcd_aux_1_b2), .B(bcd_aux_1_b3), .A(bcd_aux_1_b4), .a_2(B1), .b_2(B0), .c_2(B6),
    .d_2(B5), .e(B4), .f(B2), .g(B3));
endmodule

module BCD_AUX (
  input  A,
  input  B,
  input  C,
  input  D,
  input  E,
  input  F,
  input  G,
  input  H,
  output A3,
  output A4,
  output B1,
  output B2,
  output B3,
  output B4,
  output C1,
  output C2,
  output C3,
  output C4
);

  wire and_1_out, and_2_out, and_3_out, and_4_out, and_5_out, and_6_out, and_7_out, and_8_out, and_9_out,
       and_10_out, and_11_out, and_12_out, and_13_out, and_14_out, and_15_out, and_16_out, and_17_out,
       and_18_out, and_19_out, and_20_out, and_21_out, and_22_out, and_23_out, and_24_out, and_25_out,
       and_26_out, and_27_out, and_28_out, and_29_out, and_30_out, and_31_out, and_32_out, and_33_out,
       and_34_out, and_35_out, and_36_out, and_37_out, and_38_out, and_39_out, and_40_out, and_41_out,
       and_42_out, and_43_out, and_44_out, and_45_out, and_46_out, and_47_out, and_48_out, and_49_out,
       and_50_out, and_51_out, and_52_out, and_53_out, and_54_out, and_55_out, and_56_out, and_57_out,
       and_58_out, and_59_out, and_60_out, and_61_out, and_62_out, and_63_out, and_64_out, and_65_out,
       and_66_out, and_67_out, and_68_out, and_69_out, and_70_out, and_71_out, and_72_out, and_73_out,
       and_74_out, and_75_out, and_76_out, and_77_out, and_78_out, and_79_out, and_80_out, and_81_out,
       and_82_out, and_83_out, and_84_out, and_85_out, and_86_out, and_87_out, and_88_out, and_89_out,
       and_90_out, and_91_out, and_92_out, and_93_out, and_94_out, and_95_out, and_96_out, and_97_out,
       and_98_out, and_99_out, and_100_out, and_101_out, and_102_out, and_103_out, and_104_out, and_105_out,
       and_106_out, and_107_out, and_108_out, and_109_out, and_110_out, and_111_out, and_112_out,
       and_113_out, and_114_out, and_115_out, and_116_out, and_117_out, and_118_out, and_119_out,
       and_120_out, and_121_out, and_122_out, and_123_out, and_124_out, and_125_out, and_126_out,
       and_127_out, and_128_out, and_129_out, and_130_out, and_131_out, and_132_out, and_133_out,
       and_134_out, and_135_out, and_136_out, and_137_out, and_138_out, and_139_out, and_140_out,
       and_141_out, and_142_out, and_143_out, and_144_out, and_145_out, and_146_out, and_147_out,
       and_148_out, and_149_out, and_150_out, and_151_out, and_152_out, and_153_out, and_154_out,
       and_155_out, and_156_out, and_157_out, and_158_out, not_1_out, not_2_out, not_3_out, not_4_out,
       not_5_out, not_6_out, not_7_out, not_8_out, not_9_out, not_10_out, not_11_out, not_12_out, not_13_out,
       not_14_out, not_15_out, not_16_out, not_17_out, not_18_out, not_19_out, not_20_out, not_21_out,
       not_22_out, not_23_out, not_24_out, not_25_out, not_26_out, not_27_out, not_28_out, not_29_out,
       not_30_out, not_31_out, not_32_out, not_33_out, not_34_out, not_35_out, not_36_out, not_37_out,
       not_38_out, not_39_out, not_40_out, not_41_out, not_42_out, not_43_out, not_44_out, not_45_out,
       not_46_out, not_47_out, not_48_out, not_49_out, not_50_out, not_51_out, not_52_out, not_53_out,
       not_54_out, not_55_out, not_56_out, not_57_out, not_58_out, not_59_out, not_60_out, not_61_out,
       not_62_out, not_63_out, not_64_out, not_65_out, not_66_out, not_67_out, not_68_out, not_69_out,
       not_70_out, not_71_out, not_72_out, not_73_out, not_74_out, not_75_out, not_76_out, not_77_out,
       not_78_out, not_79_out, not_80_out, not_81_out, not_82_out, not_83_out, not_84_out, not_85_out,
       not_86_out, not_87_out, not_88_out, not_89_out, not_90_out, not_91_out, not_92_out, not_93_out,
       not_94_out, not_95_out, not_96_out, not_97_out, not_98_out, not_99_out, not_100_out, not_101_out,
       not_102_out, not_103_out, not_104_out, not_105_out, not_106_out, not_107_out, not_108_out,
       not_109_out, not_110_out, not_111_out, not_112_out, not_113_out, not_114_out, not_115_out,
       not_116_out, not_117_out, not_118_out, not_119_out, not_120_out, not_121_out, not_122_out,
       not_123_out, not_124_out, not_125_out, not_126_out, not_127_out, not_128_out, not_129_out,
       not_130_out, not_131_out, not_132_out, not_133_out, not_134_out, not_135_out, not_136_out,
       not_137_out, not_138_out, not_139_out, not_140_out, not_141_out, not_142_out, not_143_out,
       not_144_out, not_145_out, not_146_out, not_147_out, not_148_out, not_149_out, not_150_out,
       not_151_out, not_152_out, not_153_out, not_154_out, not_155_out, not_156_out, not_157_out,
       not_158_out, not_159_out, not_160_out, not_161_out, not_162_out, not_163_out, not_164_out,
       not_165_out, not_166_out, not_167_out, not_168_out, not_169_out, not_170_out, not_171_out,
       not_172_out, not_173_out, not_174_out, not_175_out, not_176_out, not_177_out, not_178_out,
       not_179_out, not_180_out, not_181_out, not_182_out, not_183_out, not_184_out, not_185_out,
       not_186_out, not_187_out, not_188_out, not_189_out, not_190_out, not_191_out, not_192_out,
       not_193_out, not_194_out, not_195_out, not_196_out, not_197_out, not_198_out, not_199_out,
       not_200_out, not_201_out, not_202_out, not_203_out, not_204_out, not_205_out, not_206_out,
       not_207_out, not_208_out, not_209_out, not_210_out, not_211_out, not_212_out, not_213_out,
       not_214_out, not_215_out, not_216_out, not_217_out, not_218_out, not_219_out, not_220_out,
       not_221_out, not_222_out, not_223_out, not_224_out, not_225_out, not_226_out, not_227_out,
       not_228_out, not_229_out, not_230_out, not_231_out, not_232_out, not_233_out, not_234_out,
       not_235_out, not_236_out, not_237_out, not_238_out, not_239_out, not_240_out, not_241_out,
       not_242_out, not_243_out, not_244_out, not_245_out, not_246_out, not_247_out, not_248_out,
       not_249_out, not_250_out, not_251_out, not_252_out, not_253_out, not_254_out, not_255_out,
       not_256_out, not_257_out, not_258_out, not_259_out, not_260_out, not_261_out, not_262_out,
       not_263_out, not_264_out, not_265_out, not_266_out, not_267_out, not_268_out, not_269_out,
       not_270_out, not_271_out, not_272_out, not_273_out, not_274_out, not_275_out, not_276_out,
       not_277_out, not_278_out, not_279_out, not_280_out, not_281_out, not_282_out, not_283_out,
       not_284_out, not_285_out, not_286_out, not_287_out, not_288_out, not_289_out, not_290_out,
       not_291_out, not_292_out, not_293_out, not_294_out, not_295_out, not_296_out, not_297_out,
       not_298_out, not_299_out, not_300_out, not_301_out, not_302_out, not_303_out, not_304_out,
       not_305_out, not_306_out, not_307_out, not_308_out, not_309_out, not_310_out, not_311_out,
       not_312_out, not_313_out, not_314_out, not_315_out, not_316_out, not_317_out, not_318_out,
       not_319_out, not_320_out, not_321_out, not_322_out, not_323_out, not_324_out, not_325_out,
       not_326_out, not_327_out, not_328_out, not_329_out, not_330_out, not_331_out, not_332_out,
       not_333_out, not_334_out, not_335_out, not_336_out, not_337_out, not_338_out, not_339_out,
       not_340_out, not_341_out, not_342_out, not_343_out, not_344_out, not_345_out, not_346_out,
       not_347_out, not_348_out, not_349_out, not_350_out, not_351_out, not_352_out, not_353_out,
       not_354_out, not_355_out, not_356_out, not_357_out, not_358_out, not_359_out, not_360_out,
       not_361_out, not_362_out, not_363_out, not_364_out, not_365_out, not_366_out, not_367_out,
       not_368_out, not_369_out, not_370_out, not_371_out, not_372_out, not_373_out, not_374_out,
       not_375_out, not_376_out, not_377_out, not_378_out, not_379_out, not_380_out, not_381_out,
       not_382_out, not_383_out, not_384_out, not_385_out, not_386_out, not_387_out, not_388_out,
       not_389_out, not_390_out, not_391_out, not_392_out, not_393_out, not_394_out, not_395_out,
       not_396_out, not_397_out, not_398_out, not_399_out, not_400_out, not_401_out, not_402_out,
       not_403_out, not_404_out, not_405_out, not_406_out, not_407_out, not_408_out, not_409_out,
       not_410_out, not_411_out, not_412_out, not_413_out, not_414_out, not_415_out, not_416_out,
       not_417_out, not_418_out, not_419_out, not_420_out, not_421_out, not_422_out, not_423_out,
       not_424_out, not_425_out, not_426_out, not_427_out, not_428_out, not_429_out, not_430_out,
       not_431_out, not_432_out, not_433_out, not_434_out, or_6_out, or_7_out, or_8_out, or_9_out;

  and and_1 (and_1_out, A, B, E);
  and and_2 (and_2_out, A, B, D);
  and and_3 (and_3_out, A, B, C);
  not not_1 (not_1_out, A);
  not not_2 (not_2_out, A);
  not not_3 (not_3_out, A);
  not not_4 (not_4_out, B);
  not not_5 (not_5_out, C);
  not not_6 (not_6_out, D);
  not not_7 (not_7_out, E);
  not not_8 (not_8_out, A);
  not not_9 (not_9_out, C);
  not not_10 (not_10_out, A);
  not not_11 (not_11_out, D);
  not not_12 (not_12_out, E);
  not not_13 (not_13_out, F);
  not not_14 (not_14_out, B);
  not not_15 (not_15_out, B);
  not not_16 (not_16_out, C);
  not not_17 (not_17_out, D);
  not not_18 (not_18_out, E);
  not not_19 (not_19_out, B);
  not not_20 (not_20_out, D);
  not not_21 (not_21_out, A);
  not not_22 (not_22_out, B);
  not not_23 (not_23_out, A);
  not not_24 (not_24_out, C);
  not not_25 (not_25_out, D);
  not not_26 (not_26_out, B);
  not not_27 (not_27_out, C);
  not not_28 (not_28_out, G);
  not not_29 (not_29_out, B);
  not not_30 (not_30_out, C);
  not not_31 (not_31_out, B);
  not not_32 (not_32_out, C);
  not not_33 (not_33_out, E);
  not not_34 (not_34_out, B);
  not not_35 (not_35_out, C);
  not not_36 (not_36_out, F);
  not not_37 (not_37_out, B);
  not not_38 (not_38_out, D);
  not not_39 (not_39_out, B);
  not not_40 (not_40_out, E);
  not not_41 (not_41_out, F);
  not not_42 (not_42_out, A);
  not not_43 (not_43_out, B);
  not not_44 (not_44_out, C);
  not not_45 (not_45_out, A);
  not not_46 (not_46_out, B);
  not not_47 (not_47_out, C);
  not not_48 (not_48_out, A);
  not not_49 (not_49_out, B);
  not not_50 (not_50_out, B);
  not not_51 (not_51_out, D);
  not not_52 (not_52_out, E);
  not not_53 (not_53_out, A);
  not not_54 (not_54_out, C);
  not not_55 (not_55_out, D);
  not not_56 (not_56_out, A);
  not not_57 (not_57_out, B);
  not not_58 (not_58_out, D);
  not not_59 (not_59_out, E);
  not not_60 (not_60_out, B);
  not not_61 (not_61_out, D);
  not not_62 (not_62_out, F);
  not not_63 (not_63_out, B);
  not not_64 (not_64_out, E);
  not not_65 (not_65_out, F);
  not not_66 (not_66_out, D);
  not not_67 (not_67_out, C);
  not not_68 (not_68_out, A);
  not not_69 (not_69_out, C);
  not not_70 (not_70_out, D);
  not not_71 (not_71_out, A);
  not not_72 (not_72_out, C);
  not not_73 (not_73_out, D);
  not not_74 (not_74_out, A);
  not not_75 (not_75_out, C);
  not not_76 (not_76_out, A);
  not not_77 (not_77_out, B);
  not not_78 (not_78_out, C);
  not not_79 (not_79_out, E);
  not not_80 (not_80_out, F);
  not not_81 (not_81_out, A);
  not not_82 (not_82_out, B);
  not not_83 (not_83_out, D);
  not not_84 (not_84_out, E);
  not not_85 (not_85_out, A);
  not not_86 (not_86_out, B);
  not not_87 (not_87_out, E);
  not not_88 (not_88_out, A);
  not not_89 (not_89_out, E);
  not not_90 (not_90_out, A);
  not not_91 (not_91_out, B);
  not not_92 (not_92_out, F);
  not not_93 (not_93_out, C);
  not not_94 (not_94_out, D);
  not not_95 (not_95_out, E);
  not not_96 (not_96_out, A);
  not not_97 (not_97_out, C);
  not not_98 (not_98_out, D);
  not not_99 (not_99_out, A);
  not not_100 (not_100_out, C);
  not not_101 (not_101_out, A);
  not not_102 (not_102_out, C);
  not not_103 (not_103_out, A);
  not not_104 (not_104_out, D);
  not not_105 (not_105_out, A);
  not not_106 (not_106_out, E);
  not not_107 (not_107_out, F);
  not not_108 (not_108_out, C);
  not not_109 (not_109_out, D);
  not not_110 (not_110_out, E);
  not not_111 (not_111_out, C);
  not not_112 (not_112_out, D);
  not not_113 (not_113_out, E);
  not not_114 (not_114_out, C);
  not not_115 (not_115_out, E);
  not not_116 (not_116_out, B);
  not not_117 (not_117_out, C);
  not not_118 (not_118_out, F);
  not not_119 (not_119_out, B);
  not not_120 (not_120_out, C);
  not not_121 (not_121_out, C);
  not not_122 (not_122_out, F);
  not not_123 (not_123_out, D);
  not not_124 (not_124_out, D);
  not not_125 (not_125_out, B);
  not not_126 (not_126_out, E);
  not not_127 (not_127_out, F);
  not not_128 (not_128_out, C);
  not not_129 (not_129_out, D);
  not not_130 (not_130_out, E);
  not not_131 (not_131_out, C);
  not not_132 (not_132_out, E);
  not not_133 (not_133_out, C);
  not not_134 (not_134_out, E);
  not not_135 (not_135_out, D);
  not not_136 (not_136_out, E);
  not not_137 (not_137_out, D);
  not not_138 (not_138_out, A);
  not not_139 (not_139_out, B);
  not not_140 (not_140_out, C);
  not not_141 (not_141_out, D);
  not not_142 (not_142_out, F);
  not not_143 (not_143_out, G);
  not not_144 (not_144_out, A);
  not not_145 (not_145_out, B);
  not not_146 (not_146_out, C);
  not not_147 (not_147_out, E);
  not not_148 (not_148_out, F);
  not not_149 (not_149_out, A);
  not not_150 (not_150_out, B);
  not not_151 (not_151_out, C);
  not not_152 (not_152_out, G);
  not not_153 (not_153_out, A);
  not not_154 (not_154_out, B);
  not not_155 (not_155_out, D);
  not not_156 (not_156_out, E);
  not not_157 (not_157_out, A);
  not not_158 (not_158_out, B);
  not not_159 (not_159_out, E);
  not not_160 (not_160_out, F);
  not not_161 (not_161_out, G);
  not not_162 (not_162_out, A);
  not not_163 (not_163_out, B);
  not not_164 (not_164_out, F);
  not not_165 (not_165_out, A);
  not not_166 (not_166_out, C);
  not not_167 (not_167_out, D);
  not not_168 (not_168_out, E);
  not not_169 (not_169_out, G);
  not not_170 (not_170_out, A);
  not not_171 (not_171_out, C);
  not not_172 (not_172_out, D);
  not not_173 (not_173_out, A);
  not not_174 (not_174_out, C);
  not not_175 (not_175_out, F);
  not not_176 (not_176_out, G);
  not not_177 (not_177_out, A);
  not not_178 (not_178_out, D);
  not not_179 (not_179_out, E);
  not not_180 (not_180_out, F);
  not not_181 (not_181_out, A);
  not not_182 (not_182_out, D);
  not not_183 (not_183_out, G);
  not not_184 (not_184_out, A);
  not not_185 (not_185_out, E);
  not not_186 (not_186_out, B);
  not not_187 (not_187_out, C);
  not not_188 (not_188_out, D);
  not not_189 (not_189_out, E);
  not not_190 (not_190_out, F);
  not not_191 (not_191_out, G);
  not not_192 (not_192_out, B);
  not not_193 (not_193_out, C);
  not not_194 (not_194_out, D);
  not not_195 (not_195_out, F);
  not not_196 (not_196_out, B);
  not not_197 (not_197_out, C);
  not not_198 (not_198_out, E);
  not not_199 (not_199_out, G);
  not not_200 (not_200_out, B);
  not not_201 (not_201_out, C);
  not not_202 (not_202_out, B);
  not not_203 (not_203_out, D);
  not not_204 (not_204_out, F);
  not not_205 (not_205_out, G);
  not not_206 (not_206_out, B);
  not not_207 (not_207_out, E);
  not not_208 (not_208_out, F);
  not not_209 (not_209_out, B);
  not not_210 (not_210_out, G);
  not not_211 (not_211_out, C);
  not not_212 (not_212_out, D);
  not not_213 (not_213_out, E);
  not not_214 (not_214_out, C);
  not not_215 (not_215_out, E);
  not not_216 (not_216_out, F);
  not not_217 (not_217_out, G);
  not not_218 (not_218_out, C);
  not not_219 (not_219_out, F);
  not not_220 (not_220_out, D);
  not not_221 (not_221_out, E);
  not not_222 (not_222_out, G);
  not not_223 (not_223_out, D);
  not not_224 (not_224_out, F);
  not not_225 (not_225_out, G);
  not not_226 (not_226_out, A);
  not not_227 (not_227_out, B);
  not not_228 (not_228_out, C);
  not not_229 (not_229_out, D);
  not not_230 (not_230_out, E);
  not not_231 (not_231_out, A);
  not not_232 (not_232_out, B);
  not not_233 (not_233_out, C);
  not not_234 (not_234_out, D);
  not not_235 (not_235_out, B);
  not not_236 (not_236_out, C);
  not not_237 (not_237_out, E);
  not not_238 (not_238_out, F);
  not not_239 (not_239_out, G);
  not not_240 (not_240_out, A);
  not not_241 (not_241_out, B);
  not not_242 (not_242_out, C);
  not not_243 (not_243_out, F);
  not not_244 (not_244_out, A);
  not not_245 (not_245_out, B);
  not not_246 (not_246_out, F);
  not not_247 (not_247_out, G);
  not not_248 (not_248_out, A);
  not not_249 (not_249_out, B);
  not not_250 (not_250_out, D);
  not not_251 (not_251_out, E);
  not not_252 (not_252_out, F);
  not not_253 (not_253_out, B);
  not not_254 (not_254_out, D);
  not not_255 (not_255_out, E);
  not not_256 (not_256_out, G);
  not not_257 (not_257_out, A);
  not not_258 (not_258_out, B);
  not not_259 (not_259_out, D);
  not not_260 (not_260_out, A);
  not not_261 (not_261_out, B);
  not not_262 (not_262_out, E);
  not not_263 (not_263_out, A);
  not not_264 (not_264_out, C);
  not not_265 (not_265_out, D);
  not not_266 (not_266_out, E);
  not not_267 (not_267_out, F);
  not not_268 (not_268_out, A);
  not not_269 (not_269_out, C);
  not not_270 (not_270_out, D);
  not not_271 (not_271_out, F);
  not not_272 (not_272_out, C);
  not not_273 (not_273_out, D);
  not not_274 (not_274_out, G);
  not not_275 (not_275_out, A);
  not not_276 (not_276_out, C);
  not not_277 (not_277_out, E);
  not not_278 (not_278_out, A);
  not not_279 (not_279_out, C);
  not not_280 (not_280_out, D);
  not not_281 (not_281_out, E);
  not not_282 (not_282_out, F);
  not not_283 (not_283_out, G);
  not not_284 (not_284_out, A);
  not not_285 (not_285_out, D);
  not not_286 (not_286_out, F);
  not not_287 (not_287_out, A);
  not not_288 (not_288_out, E);
  not not_289 (not_289_out, F);
  not not_290 (not_290_out, E);
  not not_291 (not_291_out, G);
  not not_292 (not_292_out, A);
  not not_293 (not_293_out, B);
  not not_294 (not_294_out, D);
  not not_295 (not_295_out, E);
  not not_296 (not_296_out, B);
  not not_297 (not_297_out, C);
  not not_298 (not_298_out, D);
  not not_299 (not_299_out, F);
  not not_300 (not_300_out, G);
  not not_301 (not_301_out, B);
  not not_302 (not_302_out, C);
  not not_303 (not_303_out, F);
  not not_304 (not_304_out, B);
  not not_305 (not_305_out, C);
  not not_306 (not_306_out, G);
  not not_307 (not_307_out, B);
  not not_308 (not_308_out, D);
  not not_309 (not_309_out, B);
  not not_310 (not_310_out, F);
  not not_311 (not_311_out, G);
  not not_312 (not_312_out, B);
  not not_313 (not_313_out, F);
  not not_314 (not_314_out, D);
  not not_315 (not_315_out, E);
  not not_316 (not_316_out, F);
  not not_317 (not_317_out, C);
  not not_318 (not_318_out, D);
  not not_319 (not_319_out, G);
  not not_320 (not_320_out, C);
  not not_321 (not_321_out, D);
  not not_322 (not_322_out, D);
  not not_323 (not_323_out, G);
  not not_324 (not_324_out, E);
  not not_325 (not_325_out, C);
  not not_326 (not_326_out, F);
  not not_327 (not_327_out, G);
  not not_328 (not_328_out, D);
  not not_329 (not_329_out, F);
  not not_330 (not_330_out, A);
  not not_331 (not_331_out, C);
  not not_332 (not_332_out, D);
  not not_333 (not_333_out, E);
  not not_334 (not_334_out, F);
  not not_335 (not_335_out, A);
  not not_336 (not_336_out, B);
  not not_337 (not_337_out, C);
  not not_338 (not_338_out, E);
  not not_339 (not_339_out, A);
  not not_340 (not_340_out, C);
  not not_341 (not_341_out, D);
  not not_342 (not_342_out, G);
  not not_343 (not_343_out, A);
  not not_344 (not_344_out, B);
  not not_345 (not_345_out, C);
  not not_346 (not_346_out, E);
  not not_347 (not_347_out, F);
  not not_348 (not_348_out, G);
  not not_349 (not_349_out, A);
  not not_350 (not_350_out, B);
  not not_351 (not_351_out, C);
  not not_352 (not_352_out, F);
  not not_353 (not_353_out, A);
  not not_354 (not_354_out, D);
  not not_355 (not_355_out, E);
  not not_356 (not_356_out, F);
  not not_357 (not_357_out, G);
  not not_358 (not_358_out, A);
  not not_359 (not_359_out, B);
  not not_360 (not_360_out, E);
  not not_361 (not_361_out, G);
  not not_362 (not_362_out, A);
  not not_363 (not_363_out, D);
  not not_364 (not_364_out, F);
  not not_365 (not_365_out, A);
  not not_366 (not_366_out, B);
  not not_367 (not_367_out, A);
  not not_368 (not_368_out, B);
  not not_369 (not_369_out, F);
  not not_370 (not_370_out, G);
  not not_371 (not_371_out, A);
  not not_372 (not_372_out, C);
  not not_373 (not_373_out, D);
  not not_374 (not_374_out, G);
  not not_375 (not_375_out, A);
  not not_376 (not_376_out, C);
  not not_377 (not_377_out, G);
  not not_378 (not_378_out, A);
  not not_379 (not_379_out, C);
  not not_380 (not_380_out, E);
  not not_381 (not_381_out, A);
  not not_382 (not_382_out, D);
  not not_383 (not_383_out, E);
  not not_384 (not_384_out, A);
  not not_385 (not_385_out, E);
  not not_386 (not_386_out, G);
  not not_387 (not_387_out, A);
  not not_388 (not_388_out, C);
  not not_389 (not_389_out, D);
  not not_390 (not_390_out, E);
  not not_391 (not_391_out, G);
  not not_392 (not_392_out, B);
  not not_393 (not_393_out, C);
  not not_394 (not_394_out, F);
  not not_395 (not_395_out, G);
  not not_396 (not_396_out, C);
  not not_397 (not_397_out, D);
  not not_398 (not_398_out, B);
  not not_399 (not_399_out, C);
  not not_400 (not_400_out, E);
  not not_401 (not_401_out, F);
  not not_402 (not_402_out, B);
  not not_403 (not_403_out, C);
  not not_404 (not_404_out, G);
  not not_405 (not_405_out, C);
  not not_406 (not_406_out, F);
  not not_407 (not_407_out, G);
  not not_408 (not_408_out, D);
  not not_409 (not_409_out, E);
  not not_410 (not_410_out, F);
  not not_411 (not_411_out, B);
  not not_412 (not_412_out, E);
  not not_413 (not_413_out, D);
  not not_414 (not_414_out, G);
  not not_415 (not_415_out, B);
  not not_416 (not_416_out, E);
  not not_417 (not_417_out, F);
  not not_418 (not_418_out, G);
  not not_419 (not_419_out, B);
  not not_420 (not_420_out, F);
  not not_421 (not_421_out, C);
  not not_422 (not_422_out, D);
  not not_423 (not_423_out, E);
  not not_424 (not_424_out, G);
  not not_425 (not_425_out, C);
  not not_426 (not_426_out, E);
  not not_427 (not_427_out, G);
  not not_428 (not_428_out, C);
  not not_429 (not_429_out, D);
  not not_430 (not_430_out, C);
  not not_431 (not_431_out, D);
  not not_432 (not_432_out, G);
  not not_433 (not_433_out, G);
  not not_434 (not_434_out, E);
  or or_1 (A3, and_1_out, and_2_out, and_3_out);
  and and_4 (and_4_out, not_1_out, B, C, F);
  and and_5 (and_5_out, not_2_out, B, C, E);
  and and_6 (and_6_out, not_3_out, B, C, D);
  and and_7 (and_7_out, A, not_4_out);
  and and_8 (and_8_out, A, not_5_out, not_6_out, not_7_out);
  and and_9 (and_9_out, not_8_out, B, not_9_out, D);
  and and_10 (and_10_out, not_10_out, B, C, not_11_out, not_12_out, not_13_out);
  and and_11 (and_11_out, A, not_14_out, C, D, F);
  and and_12 (and_12_out, A, not_15_out, C, D, E);
  and and_13 (and_13_out, A, B, not_16_out, not_17_out, not_18_out);
  and and_14 (and_14_out, not_19_out, C, not_20_out, E);
  and and_15 (and_15_out, not_21_out, not_22_out, C, D);
  and and_16 (and_16_out, not_23_out, B, not_24_out, not_25_out);
  and and_17 (and_17_out, A, not_26_out, not_27_out, E, F, not_28_out);
  and and_18 (and_18_out, A, not_29_out, not_30_out, E, F, H);
  and and_19 (and_19_out, A, not_31_out, not_32_out, D, not_33_out);
  and and_20 (and_20_out, A, not_34_out, not_35_out, D, not_36_out);
  and and_21 (and_21_out, A, not_37_out, C, not_38_out);
  and and_22 (and_22_out, A, not_39_out, C, not_40_out, not_41_out);
  and and_23 (and_23_out, A, B, C, D);
  and and_24 (and_24_out, not_42_out, not_43_out, not_44_out, D, F);
  and and_25 (and_25_out, not_45_out, not_46_out, not_47_out, D, E);
  and and_26 (and_26_out, not_48_out, not_49_out, D, E, F);
  and and_27 (and_27_out, not_50_out, C, not_51_out, not_52_out);
  and and_28 (and_28_out, not_53_out, B, not_54_out, not_55_out);
  and and_29 (and_29_out, not_56_out, B, C, D, E);
  and and_30 (and_30_out, A, not_57_out, not_58_out, not_59_out);
  and and_31 (and_31_out, A, not_60_out, not_61_out, not_62_out);
  and and_32 (and_32_out, A, not_63_out, C, not_64_out, not_65_out);
  and and_33 (and_33_out, A, C, not_66_out);
  and and_34 (and_34_out, A, B, not_67_out, D, E, F);
  and and_35 (and_35_out, not_68_out, not_69_out, not_70_out, E, G);
  and and_36 (and_36_out, not_71_out, not_72_out, not_73_out, E, F);
  and and_37 (and_37_out, not_74_out, not_75_out, E, F, G);
  and and_38 (and_38_out, not_76_out, not_77_out, not_78_out, D, not_79_out, not_80_out);
  and and_39 (and_39_out, not_81_out, not_82_out, C, not_83_out, not_84_out);
  and and_40 (and_40_out, not_85_out, not_86_out, C, not_87_out, G);
  and and_41 (and_41_out, not_88_out, C, D, not_89_out, F);
  and and_42 (and_42_out, not_90_out, not_91_out, C, D, E, not_92_out);
  and and_43 (and_43_out, B, not_93_out, not_94_out, not_95_out, F, G);
  and and_44 (and_44_out, not_96_out, B, not_97_out, not_98_out, E);
  and and_45 (and_45_out, not_99_out, B, not_100_out, E, G);
  and and_46 (and_46_out, not_101_out, B, not_102_out, E, F);
  and and_47 (and_47_out, not_103_out, B, not_104_out, E, F, G);
  and and_48 (and_48_out, not_105_out, B, C, not_106_out, not_107_out);
  and and_49 (and_49_out, A, not_108_out, not_109_out, not_110_out, G);
  and and_50 (and_50_out, A, not_111_out, not_112_out, not_113_out, F);
  and and_51 (and_51_out, A, not_114_out, not_115_out, F, G);
  and and_52 (and_52_out, A, not_116_out, not_117_out, E, not_118_out);
  and and_53 (and_53_out, A, not_119_out, not_120_out, D, E);
  and and_54 (and_54_out, A, not_121_out, D, E, not_122_out);
  and and_55 (and_55_out, A, C, not_123_out, E, G);
  and and_56 (and_56_out, A, C, not_124_out, E, F);
  and and_57 (and_57_out, A, C, E, F, G);
  and and_58 (and_58_out, A, not_125_out, C, D, not_126_out, not_127_out);
  and and_59 (and_59_out, A, B, not_128_out, not_129_out, not_130_out);
  and and_60 (and_60_out, A, B, not_131_out, not_132_out, G);
  and and_61 (and_61_out, A, B, not_133_out, not_134_out, F);
  and and_62 (and_62_out, A, B, not_135_out, not_136_out, F, G);
  and and_63 (and_63_out, A, B, C, not_137_out, E);
  and and_64 (and_64_out, A, B, C, E, G);
  and and_65 (and_65_out, A, B, C, E, F);
  and and_66 (and_66_out, not_138_out, not_139_out, not_140_out, not_141_out, E, not_142_out, not_143_out);
  and and_67 (and_67_out, not_144_out, not_145_out, not_146_out, D, not_147_out, not_148_out, G);
  and and_68 (and_68_out, not_149_out, not_150_out, not_151_out, D, E, F, not_152_out);
  and and_69 (and_69_out, not_153_out, not_154_out, C, not_155_out, not_156_out, F, G);
  and and_70 (and_70_out, not_157_out, not_158_out, C, D, not_159_out, not_160_out, not_161_out);
  and and_71 (and_71_out, not_162_out, not_163_out, C, D, E, not_164_out, G);
  and and_72 (and_72_out, not_165_out, B, not_166_out, not_167_out, not_168_out, F, not_169_out);
  and and_73 (and_73_out, not_170_out, B, not_171_out, not_172_out, E, F, G);
  and and_74 (and_74_out, not_173_out, B, not_174_out, D, E, not_175_out, not_176_out);
  and and_75 (and_75_out, not_177_out, B, C, not_178_out, not_179_out, not_180_out, G);
  and and_76 (and_76_out, not_181_out, B, C, not_182_out, E, F, not_183_out);
  and and_77 (and_77_out, not_184_out, B, C, D, not_185_out, F, G);
  and and_78 (and_78_out, A, not_186_out, not_187_out, not_188_out, not_189_out, not_190_out, not_191_out);
  and and_79 (and_79_out, A, not_192_out, not_193_out, not_194_out, E, not_195_out, G);
  and and_80 (and_80_out, A, not_196_out, not_197_out, D, not_198_out, F, not_199_out);
  and and_81 (and_81_out, A, not_200_out, not_201_out, D, E, F, G);
  and and_82 (and_82_out, A, not_202_out, C, not_203_out, E, not_204_out, not_205_out);
  and and_83 (and_83_out, A, not_206_out, C, D, not_207_out, not_208_out, G);
  and and_84 (and_84_out, A, not_209_out, C, D, E, F, not_210_out);
  and and_85 (and_85_out, A, B, not_211_out, not_212_out, not_213_out, F, G);
  and and_86 (and_86_out, A, B, not_214_out, D, not_215_out, not_216_out, not_217_out);
  and and_87 (and_87_out, A, B, not_218_out, D, E, not_219_out, G);
  and and_88 (and_88_out, A, B, C, not_220_out, not_221_out, F, not_222_out);
  and and_89 (and_89_out, A, B, C, not_223_out, E, F, G);
  and and_90 (and_90_out, A, B, C, D, E, not_224_out, not_225_out);
  and and_91 (and_91_out, not_226_out, not_227_out, not_228_out, not_229_out, not_230_out, F);
  and and_92 (and_92_out, not_231_out, not_232_out, not_233_out, not_234_out, F, G);
  and and_93 (and_93_out, not_235_out, not_236_out, D, not_237_out, not_238_out, not_239_out);
  and and_94 (and_94_out, not_240_out, not_241_out, not_242_out, D, E, not_243_out);
  and and_95 (and_95_out, not_244_out, not_245_out, D, E, not_246_out, not_247_out);
  and and_96 (and_96_out, not_248_out, not_249_out, C, not_250_out, not_251_out, not_252_out, G);
  and and_97 (and_97_out, not_253_out, C, not_254_out, not_255_out, F, not_256_out);
  and and_98 (and_98_out, not_257_out, not_258_out, C, not_259_out, E, F);
  and and_99 (and_99_out, not_260_out, not_261_out, C, D, not_262_out, F, G);
  and and_100 (and_100_out, not_263_out, B, not_264_out, not_265_out, not_266_out, not_267_out);
  and and_101 (and_101_out, not_268_out, B, not_269_out, not_270_out, not_271_out, G);
  and and_102 (and_102_out, B, not_272_out, not_273_out, E, F, not_274_out);
  and and_103 (and_103_out, not_275_out, B, not_276_out, D, not_277_out, F);
  and and_104 (and_104_out, not_278_out, B, not_279_out, D, F, G);
  and and_105 (and_105_out, B, C, not_280_out, not_281_out, not_282_out, not_283_out);
  and and_106 (and_106_out, not_284_out, B, C, not_285_out, E, not_286_out);
  and and_107 (and_107_out, not_287_out, B, C, D, not_288_out, not_289_out, G);
  and and_108 (and_108_out, B, C, D, not_290_out, F, not_291_out);
  and and_109 (and_109_out, not_292_out, B, C, D, E, F);
  and and_110 (and_110_out, A, not_293_out, not_294_out, not_295_out, F, G);
  and and_111 (and_111_out, A, not_296_out, not_297_out, not_298_out, E, not_299_out, not_300_out);
  and and_112 (and_112_out, A, not_301_out, not_302_out, D, not_303_out, G);
  and and_113 (and_113_out, A, not_304_out, not_305_out, D, E, F, not_306_out);
  and and_114 (and_114_out, A, not_307_out, C, not_308_out, F, G);
  and and_115 (and_115_out, A, not_309_out, C, D, not_310_out, not_311_out);
  and and_116 (and_116_out, A, not_312_out, C, D, E, not_313_out);
  and and_117 (and_117_out, A, B, not_314_out, not_315_out, not_316_out, G);
  and and_118 (and_118_out, A, B, not_317_out, not_318_out, F, not_319_out);
  and and_119 (and_119_out, A, B, not_320_out, not_321_out, E, F);
  and and_120 (and_120_out, A, B, not_322_out, E, F, not_323_out);
  and and_121 (and_121_out, A, B, D, not_324_out, F, G);
  and and_122 (and_122_out, A, B, not_325_out, D, E, not_326_out, not_327_out);
  and and_123 (and_123_out, A, B, C, not_328_out, not_329_out, G);
  and and_124 (and_124_out, A, B, C, D, F, G);
  and and_125 (and_125_out, not_330_out, not_331_out, not_332_out, not_333_out, not_334_out, G);
  and and_126 (and_126_out, not_335_out, not_336_out, not_337_out, not_338_out, F, G);
  and and_127 (and_127_out, not_339_out, not_340_out, not_341_out, E, F, not_342_out);
  and and_128 (and_128_out, not_343_out, not_344_out, not_345_out, D, not_346_out, not_347_out, not_348_out);
  and and_129 (and_129_out, not_349_out, not_350_out, not_351_out, D, E, not_352_out, G);
  and and_130 (and_130_out, not_353_out, C, not_354_out, not_355_out, not_356_out, not_357_out);
  and and_131 (and_131_out, not_358_out, not_359_out, C, not_360_out, F, not_361_out);
  and and_132 (and_132_out, not_362_out, C, not_363_out, E, not_364_out, G);
  and and_133 (and_133_out, not_365_out, not_366_out, C, E, F, G);
  and and_134 (and_134_out, not_367_out, not_368_out, C, D, E, not_369_out, not_370_out);
  and and_135 (and_135_out, not_371_out, B, not_372_out, not_373_out, E, not_374_out);
  and and_136 (and_136_out, not_375_out, B, not_376_out, E, F, not_377_out);
  and and_137 (and_137_out, not_378_out, B, not_379_out, D, not_380_out, G);
  and and_138 (and_138_out, not_381_out, B, C, not_382_out, not_383_out, F, G);
  and and_139 (and_139_out, not_384_out, B, C, D, not_385_out, not_386_out);
  and and_140 (and_140_out, not_387_out, B, C, D, E, G);
  and and_141 (and_141_out, A, not_388_out, not_389_out, not_390_out, F, not_391_out);
  and and_142 (and_142_out, A, not_392_out, not_393_out, E, not_394_out, not_395_out);
  and and_143 (and_143_out, A, not_396_out, not_397_out, E, F, G);
  and and_144 (and_144_out, A, not_398_out, not_399_out, D, not_400_out, not_401_out, G);
  and and_145 (and_145_out, A, not_402_out, not_403_out, D, E, not_404_out);
  and and_146 (and_146_out, A, not_405_out, D, E, not_406_out, not_407_out);
  and and_147 (and_147_out, A, C, not_408_out, not_409_out, not_410_out, G);
  and and_148 (and_148_out, A, not_411_out, C, not_412_out, F, G);
  and and_149 (and_149_out, A, C, not_413_out, E, F, not_414_out);
  and and_150 (and_150_out, A, not_415_out, C, D, not_416_out, not_417_out, not_418_out);
  and and_151 (and_151_out, A, not_419_out, C, D, E, not_420_out, G);
  and and_152 (and_152_out, A, B, not_421_out, not_422_out, not_423_out, not_424_out);
  and and_153 (and_153_out, A, B, not_425_out, not_426_out, F, not_427_out);
  and and_154 (and_154_out, A, B, not_428_out, not_429_out, E, G);
  and and_155 (and_155_out, A, B, not_430_out, E, F, G);
  and and_156 (and_156_out, A, B, C, not_431_out, E, not_432_out);
  and and_157 (and_157_out, A, B, C, E, F, not_433_out);
  and and_158 (and_158_out, A, B, C, D, not_434_out, G);
  or or_2 (A4, and_4_out, and_5_out, and_6_out, and_7_out, and_8_out);
  or or_3 (B1, and_9_out, and_10_out, and_11_out, and_12_out, and_13_out);
  or or_4 (B2, and_14_out, and_15_out, and_16_out, and_17_out, and_18_out, and_19_out, and_20_out, and_21_out, and_22_out, and_23_out);
  or or_5 (B3, and_24_out, and_25_out, and_26_out, and_27_out, and_28_out, and_29_out, and_30_out, and_31_out, and_32_out, and_33_out, and_34_out);
  or or_6 (or_6_out, and_91_out, and_92_out, and_93_out, and_94_out, and_95_out, and_96_out, and_97_out, and_98_out, and_99_out, and_100_out, and_101_out, and_102_out, and_103_out, and_104_out, and_105_out, and_106_out, and_107_out);
  or or_7 (or_7_out, and_108_out, and_109_out, and_110_out, and_111_out, and_112_out, and_113_out, and_114_out, and_115_out, and_116_out, and_117_out, and_118_out, and_119_out, and_120_out, and_121_out, and_122_out, and_123_out, and_124_out);
  or or_8 (or_8_out, and_125_out, and_126_out, and_127_out, and_128_out, and_129_out, and_130_out, and_131_out, and_132_out, and_133_out, and_134_out, and_135_out, and_136_out, and_137_out, and_138_out, and_139_out, and_140_out, and_141_out);
  or or_9 (or_9_out, and_142_out, and_143_out, and_144_out, and_145_out, and_146_out, and_147_out, and_148_out, and_149_out, and_150_out, and_151_out, and_152_out, and_153_out, and_154_out, and_155_out, and_156_out, and_157_out, and_158_out);
  or or_10 (B4, and_35_out, and_36_out, and_37_out, and_38_out, and_39_out, and_40_out, and_41_out, and_42_out, and_43_out, and_44_out, and_45_out, and_46_out, and_47_out, and_48_out, and_49_out, and_50_out, and_51_out, and_52_out, and_53_out, and_54_out, and_55_out, and_56_out, and_57_out, and_58_out, and_59_out, and_60_out, and_61_out, and_62_out, and_63_out, and_64_out, and_65_out);
  or or_11 (C1, and_66_out, and_67_out, and_68_out, and_69_out, and_70_out, and_71_out, and_72_out, and_73_out, and_74_out, and_75_out, and_76_out, and_77_out, and_78_out, and_79_out, and_80_out, and_81_out, and_82_out, and_83_out, and_84_out, and_85_out, and_86_out, and_87_out, and_88_out, and_89_out, and_90_out);
  or or_12 (C2, or_6_out, or_7_out);
  or or_13 (C3, or_8_out, or_9_out);

  assign C4 = H;
endmodule

module BCD_7_SEG (
  input  D,
  input  C,
  input  B,
  input  A,
  output a_2,
  output b_2,
  output c_2,
  output d_2,
  output e,
  output f,
  output g
);

  wire nand_1_out, nand_2_out, nand_3_out, nand_4_out, nand_5_out, nand_6_out, nand_7_out, nand_8_out,
       nand_9_out, nand_10_out, nand_11_out, nand_12_out, nand_13_out, nand_14_out, nand_15_out, nand_16_out,
       nand_17_out, nand_18_out, nand_19_out, nand_20_out, nand_21_out, nand_22_out, nand_23_out,
       nand_24_out, nand_25_out, nand_26_out, nand_27_out, nand_28_out, nand_29_out, nand_30_out,
       nand_31_out, nand_32_out, nand_33_out, nand_34_out, nand_35_out, nand_36_out, nand_37_out,
       nand_38_out, nand_39_out, nand_40_out, nand_41_out, nand_42_out, nand_43_out, nand_44_out,
       nand_45_out, nand_46_out, nand_47_out, nand_48_out, nand_49_out, nand_50_out, nand_51_out,
       nand_52_out, nand_53_out, nand_54_out, nand_55_out, nand_56_out, nand_57_out, nand_58_out,
       nand_59_out, nand_60_out, nand_61_out, nand_62_out, nand_63_out, nand_64_out, nand_65_out,
       nand_66_out, nand_67_out, nand_68_out, nand_69_out, nand_70_out, nand_71_out, nand_72_out,
       nand_73_out, nand_74_out, nand_75_out, nand_76_out, nand_77_out, nand_78_out, nand_79_out,
       nand_80_out, nand_81_out, nand_82_out, nand_83_out, nand_84_out, nand_85_out, nand_86_out,
       nand_87_out, nand_88_out, nand_89_out, nand_90_out, nand_91_out, nand_92_out, nand_93_out,
       nand_94_out, nand_95_out, nand_96_out, nand_97_out, nand_98_out, nand_99_out, nand_100_out,
       nand_101_out, nand_102_out, nand_103_out, nand_104_out, nand_106_out, nand_107_out, nand_108_out,
       nand_109_out, nand_110_out, nand_111_out, nand_112_out, nand_113_out, nand_114_out, nand_115_out,
       nand_116_out, nand_117_out, nand_118_out, nand_119_out, nand_120_out, nand_121_out, nand_122_out,
       nand_123_out, nand_124_out, nand_125_out, nand_126_out, nand_127_out, nand_128_out, nand_129_out,
       nand_130_out, nand_131_out, nand_132_out, nand_133_out, nand_134_out, nand_136_out, nand_137_out,
       nand_138_out, nand_139_out, nand_141_out, nand_142_out, nand_143_out, nand_144_out, nand_145_out,
       nand_146_out, nand_147_out, nand_148_out;

  nand nand_1 (nand_1_out, C, C);
  nand nand_2 (nand_2_out, D, D);
  nand nand_3 (nand_3_out, B, B);
  nand nand_4 (nand_4_out, D, D);
  nand nand_5 (nand_5_out, B, B);
  nand nand_6 (nand_6_out, D, D);
  nand nand_7 (nand_7_out, D, D);
  nand nand_8 (nand_8_out, C, C);
  nand nand_9 (nand_9_out, C, C);
  nand nand_10 (nand_10_out, C, C);
  nand nand_11 (nand_11_out, A, A);
  nand nand_12 (nand_12_out, A, A);
  nand nand_13 (nand_13_out, D, D);
  nand nand_14 (nand_14_out, C, C);
  nand nand_15 (nand_15_out, A, A);
  nand nand_16 (nand_16_out, D, D);
  nand nand_17 (nand_17_out, D, nand_1_out);
  nand nand_18 (nand_18_out, nand_2_out, nand_3_out);
  nand nand_19 (nand_19_out, nand_4_out, nand_5_out);
  nand nand_20 (nand_20_out, nand_6_out, A);
  nand nand_21 (nand_21_out, nand_7_out, nand_8_out);
  nand nand_22 (nand_22_out, nand_9_out, B);
  nand nand_23 (nand_23_out, nand_10_out, nand_11_out);
  nand nand_24 (nand_24_out, B, nand_12_out);
  nand nand_25 (nand_25_out, D, B);
  nand nand_26 (nand_26_out, D, C);
  nand nand_27 (nand_27_out, nand_13_out, C);
  nand nand_28 (nand_28_out, nand_14_out, B);
  nand nand_29 (nand_29_out, B, nand_15_out);
  nand nand_30 (nand_30_out, nand_16_out, C);
  nand nand_31 (nand_31_out, C, C);
  nand nand_32 (nand_32_out, A, A);
  nand nand_33 (nand_33_out, D, D);
  nand nand_34 (nand_34_out, D, D);
  nand nand_35 (nand_35_out, nand_17_out, nand_17_out);
  nand nand_36 (nand_36_out, B, B);
  nand nand_37 (nand_37_out, D, D);
  nand nand_38 (nand_38_out, C, C);
  nand nand_39 (nand_39_out, nand_18_out, nand_18_out);
  nand nand_40 (nand_40_out, A, A);
  nand nand_41 (nand_41_out, D, D);
  nand nand_42 (nand_42_out, B, B);
  nand nand_43 (nand_43_out, nand_19_out, nand_20_out);
  nand nand_44 (nand_44_out, B, B);
  nand nand_45 (nand_45_out, D, D);
  nand nand_46 (nand_46_out, C, C);
  nand nand_47 (nand_47_out, nand_21_out, nand_21_out);
  nand nand_48 (nand_48_out, A, A);
  nand nand_49 (nand_49_out, nand_22_out, nand_22_out);
  nand nand_50 (nand_50_out, B, B);
  nand nand_51 (nand_51_out, B, B);
  nand nand_52 (nand_52_out, nand_23_out, nand_24_out);
  nand nand_53 (nand_53_out, nand_25_out, nand_26_out);
  nand nand_54 (nand_54_out, B, B);
  nand nand_55 (nand_55_out, A, A);
  nand nand_56 (nand_56_out, nand_27_out, nand_27_out);
  nand nand_57 (nand_57_out, B, B);
  nand nand_58 (nand_58_out, nand_28_out, nand_29_out);
  nand nand_59 (nand_59_out, nand_30_out, nand_30_out);
  nand nand_60 (nand_60_out, B, B);
  nand nand_61 (nand_61_out, C, C);
  nand nand_62 (nand_62_out, nand_31_out, nand_32_out);
  nand nand_63 (nand_63_out, nand_33_out, B);
  nand nand_64 (nand_64_out, nand_34_out, C);
  nand nand_65 (nand_65_out, C, B);
  nand nand_66 (nand_66_out, nand_35_out, nand_36_out);
  nand nand_67 (nand_67_out, nand_37_out, nand_38_out);
  nand nand_68 (nand_68_out, nand_39_out, nand_40_out);
  nand nand_69 (nand_69_out, nand_41_out, B);
  nand nand_70 (nand_70_out, D, nand_42_out);
  nand nand_71 (nand_71_out, nand_43_out, nand_43_out);
  nand nand_72 (nand_72_out, nand_44_out, A);
  nand nand_73 (nand_73_out, nand_45_out, C);
  nand nand_74 (nand_74_out, D, nand_46_out);
  nand nand_75 (nand_75_out, nand_47_out, nand_48_out);
  nand nand_76 (nand_76_out, nand_49_out, A);
  nand nand_77 (nand_77_out, C, nand_50_out);
  nand nand_78 (nand_78_out, C, B);
  nand nand_79 (nand_79_out, D, nand_51_out);
  nand nand_80 (nand_80_out, nand_52_out, nand_52_out);
  nand nand_81 (nand_81_out, nand_53_out, nand_53_out);
  nand nand_82 (nand_82_out, nand_54_out, nand_55_out);
  nand nand_83 (nand_83_out, nand_56_out, nand_57_out);
  nand nand_84 (nand_84_out, nand_58_out, nand_58_out);
  nand nand_85 (nand_85_out, nand_59_out, nand_60_out);
  nand nand_86 (nand_86_out, D, nand_61_out);
  nand nand_87 (nand_87_out, D, A);
  nand nand_88 (nand_88_out, nand_62_out, nand_63_out);
  nand nand_89 (nand_89_out, nand_64_out, nand_64_out);
  nand nand_90 (nand_90_out, nand_65_out, nand_66_out);
  nand nand_91 (nand_91_out, A, A);
  nand nand_92 (nand_92_out, nand_67_out, nand_68_out);
  nand nand_93 (nand_93_out, C, C);
  nand nand_94 (nand_94_out, A, A);
  nand nand_95 (nand_95_out, nand_69_out, nand_69_out);
  nand nand_96 (nand_96_out, nand_70_out, nand_70_out);
  nand nand_97 (nand_97_out, nand_71_out, nand_72_out);
  nand nand_98 (nand_98_out, nand_73_out, nand_74_out);
  nand nand_99 (nand_99_out, nand_75_out, nand_76_out);
  nand nand_100 (nand_100_out, nand_77_out, nand_77_out);
  nand nand_101 (nand_101_out, nand_78_out, nand_78_out);
  nand nand_102 (nand_102_out, A, A);
  nand nand_103 (nand_103_out, nand_79_out, nand_79_out);
  nand nand_104 (nand_104_out, A, A);
  nand nand_105 (e, nand_80_out, nand_81_out);
  nand nand_106 (nand_106_out, nand_82_out, nand_83_out);
  nand nand_107 (nand_107_out, A, A);
  nand nand_108 (nand_108_out, C, C);
  nand nand_109 (nand_109_out, nand_84_out, nand_85_out);
  nand nand_110 (nand_110_out, nand_86_out, nand_87_out);
  nand nand_111 (nand_111_out, nand_88_out, nand_88_out);
  nand nand_112 (nand_112_out, nand_89_out, A);
  nand nand_113 (nand_113_out, nand_90_out, nand_90_out);
  nand nand_114 (nand_114_out, D, nand_91_out);
  nand nand_115 (nand_115_out, nand_92_out, nand_92_out);
  nand nand_116 (nand_116_out, nand_93_out, nand_94_out);
  nand nand_117 (nand_117_out, nand_95_out, A);
  nand nand_118 (nand_118_out, nand_96_out, A);
  nand nand_119 (nand_119_out, nand_97_out, nand_97_out);
  nand nand_120 (nand_120_out, nand_98_out, nand_98_out);
  nand nand_121 (nand_121_out, nand_99_out, nand_99_out);
  nand nand_122 (nand_122_out, nand_100_out, A);
  nand nand_123 (nand_123_out, nand_101_out, nand_102_out);
  nand nand_124 (nand_124_out, nand_103_out, nand_104_out);
  nand nand_125 (nand_125_out, nand_106_out, nand_106_out);
  nand nand_126 (nand_126_out, C, nand_107_out);
  nand nand_127 (nand_127_out, D, nand_108_out);
  nand nand_128 (nand_128_out, D, B);
  nand nand_129 (nand_129_out, nand_109_out, nand_109_out);
  nand nand_130 (nand_130_out, nand_110_out, nand_110_out);
  nand nand_131 (nand_131_out, nand_111_out, nand_112_out);
  nand nand_132 (nand_132_out, nand_113_out, nand_114_out);
  nand nand_133 (nand_133_out, nand_115_out, nand_116_out);
  nand nand_134 (nand_134_out, nand_117_out, nand_118_out);
  nand nand_135 (c_2, nand_119_out, nand_120_out);
  nand nand_136 (nand_136_out, nand_121_out, nand_122_out);
  nand nand_137 (nand_137_out, nand_123_out, nand_124_out);
  nand nand_138 (nand_138_out, nand_125_out, nand_126_out);
  nand nand_139 (nand_139_out, nand_127_out, nand_128_out);
  nand nand_140 (g, nand_129_out, nand_130_out);
  nand nand_141 (nand_141_out, nand_131_out, nand_131_out);
  nand nand_142 (nand_142_out, nand_132_out, nand_132_out);
  nand nand_143 (nand_143_out, nand_133_out, nand_133_out);
  nand nand_144 (nand_144_out, nand_134_out, nand_134_out);
  nand nand_145 (nand_145_out, nand_136_out, nand_136_out);
  nand nand_146 (nand_146_out, nand_137_out, nand_137_out);
  nand nand_147 (nand_147_out, nand_138_out, nand_138_out);
  nand nand_148 (nand_148_out, nand_139_out, nand_139_out);
  nand nand_149 (a_2, nand_141_out, nand_142_out);
  nand nand_150 (b_2, nand_143_out, nand_144_out);
  nand nand_151 (d_2, nand_145_out, nand_146_out);
  nand nand_152 (f, nand_147_out, nand_148_out);
endmodule
