// Logisim project CPU MIPS 16 BITS FINAL.circ as structural Verilog: 11 circuits, main circuit main
// ll
module main (
  input  ON_OFF,
  output [7:0] S0,
  output [7:0] S1,
  output [7:0] S2,
  output [7:0] T0,
  output [7:0] T1,
  output [7:0] D0,
  output [7:0] D1
);

  wire CLOCK_out, cpu_1_read_mem, cpu_1_write_mem, RESET_out;
  wire [3:0] show_instr_1_mais_sign, show_instr_1_menos_sign, show_instr_1_out_3, show_instr_1_out_4,
       show_instr_1_out_5, show_instr_1_out_6, show_instr_1_out_7, show_instr_1_out_8, show_instr_1_out_9,
       show_instr_1_out_10, show_instr_1_out_11, show_instr_1_out_12, show_instr_1_out_13,
       show_instr_1_out_14, show_instr_1_out_15, show_instr_1_out_16;
  wire [15:0] INSTR;

  LED READ (.in(cpu_1_read_mem));
  Button RESET (.out(RESET_out));
  Hex_Digit_Display hex_digit_display_1 (.value(show_instr_1_out_3));  // open: dp
  Hex_Digit_Display hex_digit_display_2 (.value(show_instr_1_mais_sign));  // open: dp
  SHOW_INSTR show_instr_1 (
    .Input(INSTR), .mais_sign(show_instr_1_mais_sign), .out_3(show_instr_1_out_3),
    .out_4(show_instr_1_out_4), .out_5(show_instr_1_out_5), .out_6(show_instr_1_out_6),
    .out_7(show_instr_1_out_7), .out_8(show_instr_1_out_8), .out_9(show_instr_1_out_9),
    .out_10(show_instr_1_out_10), .out_11(show_instr_1_out_11), .out_12(show_instr_1_out_12),
    .out_13(show_instr_1_out_13), .out_14(show_instr_1_out_14), .out_15(show_instr_1_out_15),
    .out_16(show_instr_1_out_16), .menos_sign(show_instr_1_menos_sign));
  LED WRITE (.in(cpu_1_write_mem));
  CPU cpu_1 (
    .ON_OFF(ON_OFF), .RESET(RESET_out), .CLOCK(CLOCK_out), .WRITE_MEM(cpu_1_write_mem),
    .READ_MEM(cpu_1_read_mem), .INSTRUCTION(INSTR), .S0(S0), .S1(S1), .S2(S2), .D1(D1), .T0(T0), .T1(T1),
    .D0(D0));
  Hex_Digit_Display hex_digit_display_3 (.value(show_instr_1_out_4));  // open: dp
  Hex_Digit_Display hex_digit_display_4 (.value(show_instr_1_out_5));  // open: dp
  Clock CLOCK (.out(CLOCK_out));
  Hex_Digit_Display hex_digit_display_5 (.value(show_instr_1_out_7));  // open: dp
  Hex_Digit_Display hex_digit_display_6 (.value(show_instr_1_out_6));  // open: dp
  Hex_Digit_Display hex_digit_display_7 (.value(show_instr_1_out_8));  // open: dp
  Hex_Digit_Display hex_digit_display_8 (.value(show_instr_1_out_9));  // open: dp
  Hex_Digit_Display hex_digit_display_9 (.value(show_instr_1_out_10));  // open: dp
  Hex_Digit_Display hex_digit_display_10 (.value(show_instr_1_out_11));  // open: dp
  Hex_Digit_Display hex_digit_display_11 (.value(show_instr_1_out_12));  // open: dp
  Hex_Digit_Display hex_digit_display_12 (.value(show_instr_1_out_14));  // open: dp
  Hex_Digit_Display hex_digit_display_13 (.value(show_instr_1_out_13));  // open: dp
  Hex_Digit_Display hex_digit_display_14 (.value(show_instr_1_out_15));  // open: dp
  Hex_Digit_Display hex_digit_display_15 (.value(show_instr_1_out_16));  // open: dp
  Hex_Digit_Display hex_digit_display_16 (.value(show_instr_1_menos_sign));  // open: dp
endmodule

// count
module COUNT (
  input  [3:0] plus_1,
  input  Enable,
  input  Clear,
  input  Clock,
  output [3:0] Out
);

  wire [3:0] adder_1_out;

  Adder #(.width(4)) adder_1 (.a(Out), .b(plus_1), .out(adder_1_out));  // open: cin, cout
  Register #(.width(4)) register_1 (.D(adder_1_out), .en(Enable), .Q(Out), .clk(Clock), .clr(Clear));
endmodule

module CONTROLLER (
  input  on_off,
  input  [7:0] load_mem_data,
  input  [3:0] pc_out,
  input  [15:0] data_instr,
  input  Reset,
  input  CLOCK,
  input  [7:0] alu_out,
  input  [7:0] r1_out,
  input  [7:0] r2_out,
  output [7:0] write_mem_data,
  output [7:0] mem_data_adrress,
  output mem_s_r,
  output mem_cl,
  output cpi_en,
  output pc_en,
  output pc_cl,
  output [3:0] pc_in,
  output r_en,
  output r_cl,
  output [7:0] alu_a,
  output [7:0] alu_b,
  output [2:0] alu_op,
  output alu_en,
  output [2:0] r1_select,
  output [2:0] r2_select,
  output [2:0] r_data_select,
  output REG_EN_WRITE,
  output [7:0] REG_DATA,
  output regs_cl
);

  wire adder_1_cout, and_1_out, and_2_out, and_3_out, comparator_1_eq, comparator_2_lt, DMX_r2_out, I_011,
       I_100, I_101, I_110, J_111, MUX_r1_select, MUX_r2_select, MUX_r_data_select, MUX_ula_b, MUX_ula_op,
       nor_1_out, nor_5_out, not_2_out, not_3_out, or_1_out, or_4_out, R_000, R_001, R_010, REG_ULA_EN,
       SHIFT_R;
  wire [1:0] MUX_I, MUX_R, MUX_reg_data;
  wire [2:0] FUNC_R, RD_R, RS_I, RS_R, RT_I, RT_R;
  wire [3:0] adder_1_out, ADDR_J, bit_extender_3_out;
  wire [7:0] A_B, IMM_I, R2_OUT_B, RESULT_LESS, RESULT_SHIFT;
  wire [15:0] demultiplexer_1_out0, demultiplexer_1_out1, demultiplexer_1_out2, demultiplexer_1_out3,
       demultiplexer_1_out4, demultiplexer_1_out5, demultiplexer_1_out6, demultiplexer_1_out7,
       multiplexer_6_out;
  wire [15:13] multiplexer_5_out;

  nor nor_1 (nor_1_out, I_100, I_101, J_111);
  or or_1 (or_1_out, R_000, I_011, I_100, I_110);
  nor nor_2 (MUX_ula_op, R_000, R_001, R_010);
  nor nor_3 (MUX_r1_select, R_000, R_001, R_010);
  nor nor_4 (MUX_r2_select, R_000, R_001, R_010);
  or or_2 (MUX_r_data_select, I_011, I_110);
  or or_3 (MUX_ula_b, I_011, I_100, I_110);
  or or_4 (or_4_out, R_000, I_100, I_101, I_110, J_111);
  not not_1 (DMX_r2_out, R_000);
  PORT_AND port_and_1 (
    .in_1(1'b1), .in_2(1'b1), .in_3(nor_1_out), .in_4(or_1_out), .in_5(or_1_out), .COMUM(on_off),
    .out_1(pc_en), .out_2(r_en), .out_3(REG_EN_WRITE), .out_4(REG_ULA_EN), .out_5(alu_en));  // open: in_6, in_7, in_8, in_9, in_10, in_11, in_12, in_13, in_14, out_6, out_7, out_8, out_9, out_10, out_11, out_12, out_13, out_14
  assign MUX_reg_data = or_4_out ? 2'b00 : 2'bz;  // Controlled_Buffer controlled_buffer_1
  assign MUX_R = R_000 ? 2'b00 : 2'bz;  // Controlled_Buffer controlled_buffer_2
  assign MUX_I = I_011 ? 2'b00 : 2'bz;  // Controlled_Buffer controlled_buffer_3
  assign MUX_reg_data = R_001 ? 2'b01 : 2'bz;  // Controlled_Buffer controlled_buffer_4
  assign MUX_reg_data = R_010 ? 2'b10 : 2'bz;  // Controlled_Buffer controlled_buffer_5
  assign MUX_R = R_001 ? 2'b01 : 2'bz;  // Controlled_Buffer controlled_buffer_6
  assign MUX_R = R_010 ? 2'b10 : 2'bz;  // Controlled_Buffer controlled_buffer_7
  assign MUX_I = I_100 ? 2'b01 : 2'bz;  // Controlled_Buffer controlled_buffer_8
  assign MUX_I = I_101 ? 2'b10 : 2'bz;  // Controlled_Buffer controlled_buffer_9
  assign MUX_reg_data = I_011 ? 2'b11 : 2'bz;  // Controlled_Buffer controlled_buffer_10
  assign MUX_I = I_110 ? 2'b11 : 2'bz;  // Controlled_Buffer controlled_buffer_11
  Multiplexer #(.width(3)) multiplexer_1 (.in0(RS_R), .in1(RS_I), .out(r1_select), .sel(MUX_r1_select), .en(1'b1));
  Multiplexer #(.width(3)) multiplexer_2 (.in0(RT_R), .in1(RT_I), .out(r2_select), .sel(MUX_r2_select), .en(1'b1));
  PORT_AND port_and_2 (
    .in_1(1'b1), .in_2(1'b1), .in_3(1'b1), .in_4(1'b1), .in_5(1'b1), .in_6(1'b1), .in_7(1'b1), .in_8(1'b1),
    .in_9(1'b1), .in_10(1'b1), .in_11(1'b1), .in_12(1'b1), .in_13(1'b1), .in_14(1'b1), .COMUM(Reset),
    .out_1(pc_cl), .out_2(r_cl), .out_3(regs_cl), .out_4(mem_cl));  // open: out_5, out_6, out_7, out_8, out_9, out_10, out_11, out_12, out_13, out_14
  Multiplexer #(.width(3)) multiplexer_3 (
    .in0(RD_R), .in1(RT_I), .out(r_data_select), .sel(MUX_r_data_select), .en(1'b1));
  Multiplexer #(.select(2), .width(8)) multiplexer_4 (
    .in0(A_B), .in1(RESULT_SHIFT), .in2(RESULT_LESS), .in3(load_mem_data), .out(REG_DATA),
    .sel(MUX_reg_data), .en(1'b1));
  Demultiplexer #(.select(3), .width(16)) demultiplexer_1 (
    .out0(demultiplexer_1_out0), .out1(demultiplexer_1_out1), .out2(demultiplexer_1_out2),
    .out3(demultiplexer_1_out3), .out4(demultiplexer_1_out4), .out5(demultiplexer_1_out5),
    .out6(demultiplexer_1_out6), .out7(demultiplexer_1_out7), .in(data_instr), .sel(data_instr[15:13]),
    .en(1'b1));
  Decoder #(.select(3), .enable("false")) decoder_1 (
    .out0(R_000), .out1(R_001), .out2(R_010), .out3(I_011), .out4(I_100), .out5(I_101), .out6(I_110),
    .out7(J_111), .sel(data_instr[15:13]));
  Multiplexer #(.select(2), .width(16)) multiplexer_5 (
    .in0(demultiplexer_1_out0), .in1(demultiplexer_1_out1), .in2(demultiplexer_1_out2),
    .out({multiplexer_5_out, RS_R, RT_R, RD_R, SHIFT_R, FUNC_R}), .sel(MUX_R), .en(1'b1));  // open: in3
  Multiplexer #(.select(2), .width(16)) multiplexer_6 (
    .in0(demultiplexer_1_out3), .in1(demultiplexer_1_out4), .in2(demultiplexer_1_out5),
    .in3(demultiplexer_1_out6), .out({multiplexer_6_out[15:13], RS_I, RT_I, multiplexer_6_out[6:0]}),
    .sel(MUX_I), .en(1'b1));
  Demultiplexer #(.width(8)) demultiplexer_2 (
    .out0(R2_OUT_B), .out1(write_mem_data), .in(r2_out), .sel(DMX_r2_out), .en(1'b1));
  assign mem_data_adrress = and_1_out ? {8{1'b0}} : 8'bz;  // Controlled_Buffer controlled_buffer_12
  and and_1 (and_1_out, not_2_out, not_3_out);
  Bit_Extender #(.in_width(13), .out_width(4)) bit_extender_1 (.in(demultiplexer_1_out7[12:0]), .out(ADDR_J));
  not not_2 (not_2_out, and_2_out);
  assign IMM_I = {{1{1'b0}}, multiplexer_6_out[6:0]};  // Bit_Extender bit_extender_2
  assign mem_data_adrress = and_2_out ? A_B : 8'bz;  // Controlled_Buffer controlled_buffer_13
  not not_3 (not_3_out, I_100);
  and and_2 (and_2_out, not_3_out, I_011);
  assign mem_data_adrress = I_100 ? alu_out : 8'bz;  // Controlled_Buffer controlled_buffer_14
  not not_4 (mem_s_r, I_100);
  Multiplexer #(.width(8)) multiplexer_7 (.in0(R2_OUT_B), .in1(IMM_I), .out(alu_b), .sel(MUX_ula_b), .en(1'b1));
  Multiplexer #(.width(3)) multiplexer_8 (.in0(FUNC_R), .in1(3'b000), .out(alu_op), .sel(MUX_ula_op), .en(1'b1));
  Comparator comparator_1 (.a(r1_out), .b(write_mem_data), .eq(comparator_1_eq));  // open: gt, lt
  Shifter shifter_1 (.in(write_mem_data), .\dist (RS_R), .out(RESULT_SHIFT));
  Comparator comparator_2 (.a(r1_out), .b(write_mem_data), .lt(comparator_2_lt));  // open: gt, eq
  assign pc_in = and_3_out ? bit_extender_3_out : 4'bz;  // Controlled_Buffer controlled_buffer_15
  Bit_Extender #(.out_width(4)) bit_extender_3 (.in(IMM_I), .out(bit_extender_3_out));
  and and_3 (and_3_out, comparator_1_eq, I_101);
  Multiplexer #(.width(8)) multiplexer_9 (
    .in0({8{1'b0}}), .in1(8'h1), .out(RESULT_LESS), .sel(comparator_2_lt), .en(1'b1));
  Register register_1 (.D(alu_out), .en(REG_ULA_EN), .Q(A_B), .clk(CLOCK));  // open: clr
  not not_5 (cpi_en, adder_1_cout);
  assign pc_in = nor_5_out ? adder_1_out : 4'bz;  // Controlled_Buffer controlled_buffer_16
  Adder #(.width(4)) adder_1 (.a(pc_out), .b(4'b0001), .out(adder_1_out), .cout(adder_1_cout));  // open: cin
  nor nor_5 (nor_5_out, and_3_out, J_111);
  assign pc_in = J_111 ? ADDR_J : 4'bz;  // Controlled_Buffer controlled_buffer_17

  assign alu_a = r1_out;

  // Other names for the same wires on the sheet: LOAD[7:0] = load_mem_data; R2_OUT_t[7:0] = write_mem_data;
  //   REG_EN_W = REG_EN_WRITE; RI_CL = r_cl; RI_EN = r_en; RS_IMM[7:0] = alu_out; ULA_EN = alu_en
endmodule

module ALU (
  input  [7:0] IN_A,
  input  [7:0] IN_B,
  input  [2:0] Select,
  input  Enable,
  output [7:0] OUT
);

  wire [7:0] adder_1_out, and_1_out, divider_1_out, multiplier_1_out, not_1_out, or_1_out, subtractor_1_out,
       undriven;

  Adder adder_1 (.a(IN_A), .b(IN_B), .out(adder_1_out));  // open: cin, cout
  Subtractor subtractor_1 (.a(IN_A), .b(IN_B), .out(subtractor_1_out));  // open: bin, bout
  Multiplier multiplier_1 (.a(IN_A), .b(IN_B), .out(multiplier_1_out));  // open: cin, cout
  Divider divider_1 (.a(IN_A), .b(IN_B), .out(divider_1_out));  // open: upper, rem
  assign and_1_out = IN_A & IN_B;  // AND_Gate and_1, 8 bits wide
  assign or_1_out = IN_A | IN_B;  // OR_Gate or_1, 8 bits wide
  assign not_1_out = ~IN_A;  // NOT_Gate not_1, 8 bits wide
  Multiplexer #(.select(3), .width(8)) multiplexer_1 (
    .in0(adder_1_out), .in1(subtractor_1_out), .in2(multiplier_1_out), .in3(divider_1_out), .in4(and_1_out),
    .in5(or_1_out), .in6(not_1_out), .in7(undriven), .out(OUT), .sel(Select), .en(Enable));
endmodule

// REGITERS
module REGISTERS (
  input  [7:0] DATA,
  input  CLOCK,
  input  CLEAR,
  input  [2:0] SELECT_OUT_1,
  input  [2:0] SELECT_OUT_2,
  input  ENABLE,
  input  [2:0] SELECT_WRITE,
  output [7:0] OUT_1,
  output [7:0] OUT_2
);

  wire demultiplexer_2_out0, demultiplexer_2_out1, demultiplexer_2_out2, demultiplexer_2_out3,
       demultiplexer_2_out4, demultiplexer_2_out5, demultiplexer_2_out6, demultiplexer_2_out7;
  wire [7:0] demultiplexer_1_out1, demultiplexer_1_out2, demultiplexer_1_out3, demultiplexer_1_out4,
       demultiplexer_1_out5, demultiplexer_1_out6, demultiplexer_1_out7, register_1_q, register_2_q,
       register_3_q, register_4_q, register_5_q, register_6_q, register_7_q, register_8_q;

  Demultiplexer #(.select(3), .width(8)) demultiplexer_1 (
    .out1(demultiplexer_1_out1), .out2(demultiplexer_1_out2), .out3(demultiplexer_1_out3),
    .out4(demultiplexer_1_out4), .out5(demultiplexer_1_out5), .out6(demultiplexer_1_out6),
    .out7(demultiplexer_1_out7), .in(DATA), .sel(SELECT_WRITE), .en(1'b1));  // open: out0
  Demultiplexer #(.select(3)) demultiplexer_2 (
    .out0(demultiplexer_2_out0), .out1(demultiplexer_2_out1), .out2(demultiplexer_2_out2),
    .out3(demultiplexer_2_out3), .out4(demultiplexer_2_out4), .out5(demultiplexer_2_out5),
    .out6(demultiplexer_2_out6), .out7(demultiplexer_2_out7), .in(ENABLE), .sel(SELECT_WRITE), .en(1'b1));
  Register register_1 (.D(demultiplexer_1_out7), .en(demultiplexer_2_out7), .Q(register_1_q), .clk(CLOCK), .clr(CLEAR));
  Register register_2 (.D(demultiplexer_1_out6), .en(demultiplexer_2_out6), .Q(register_2_q), .clk(CLOCK), .clr(CLEAR));
  Register register_3 (.D(demultiplexer_1_out5), .en(demultiplexer_2_out5), .Q(register_3_q), .clk(CLOCK), .clr(CLEAR));
  Register register_4 (.D(demultiplexer_1_out4), .en(demultiplexer_2_out4), .Q(register_4_q), .clk(CLOCK), .clr(CLEAR));
  Register register_5 (.D(demultiplexer_1_out3), .en(demultiplexer_2_out3), .Q(register_5_q), .clk(CLOCK), .clr(CLEAR));
  Register register_6 (.D(demultiplexer_1_out2), .en(demultiplexer_2_out2), .Q(register_6_q), .clk(CLOCK), .clr(CLEAR));
  Register register_7 (.D(demultiplexer_1_out1), .en(demultiplexer_2_out1), .Q(register_7_q), .clk(CLOCK), .clr(CLEAR));
  Register register_8 (.D({8{1'b0}}), .en(demultiplexer_2_out0), .Q(register_8_q), .clk(CLOCK), .clr(CLEAR));
  Multiplexer #(.select(3), .width(8)) multiplexer_1 (
    .in0(register_8_q), .in1(register_7_q), .in2(register_6_q), .in3(register_5_q), .in4(register_4_q),
    .in5(register_3_q), .in6(register_2_q), .in7(register_1_q), .out(OUT_1), .sel(SELECT_OUT_1), .en(1'b1));
  Multiplexer #(.select(3), .width(8)) multiplexer_2 (
    .in0(register_8_q), .in1(register_7_q), .in2(register_6_q), .in3(register_5_q), .in4(register_4_q),
    .in5(register_3_q), .in6(register_2_q), .in7(register_1_q), .out(OUT_2), .sel(SELECT_OUT_2), .en(1'b1));
endmodule

module SHOW_INSTR (
  input  [15:0] Input,
  output [3:0] mais_sign,
  output [3:0] out_3,
  output [3:0] out_4,
  output [3:0] out_5,
  output [3:0] out_6,
  output [3:0] out_7,
  output [3:0] out_8,
  output [3:0] out_9,
  output [3:0] out_10,
  output [3:0] out_11,
  output [3:0] out_12,
  output [3:0] out_13,
  output [3:0] out_14,
  output [3:0] out_15,
  output [3:0] out_16,
  output [3:0] menos_sign
);

  assign menos_sign = {{3{1'b0}}, Input[0]};  // Bit_Extender bit_extender_1
  assign out_16 = {{3{1'b0}}, Input[1]};  // Bit_Extender bit_extender_2
  assign out_15 = {{3{1'b0}}, Input[2]};  // Bit_Extender bit_extender_3
  assign out_14 = {{3{1'b0}}, Input[3]};  // Bit_Extender bit_extender_4
  assign out_13 = {{3{1'b0}}, Input[4]};  // Bit_Extender bit_extender_5
  assign out_12 = {{3{1'b0}}, Input[5]};  // Bit_Extender bit_extender_6
  assign out_11 = {{3{1'b0}}, Input[6]};  // Bit_Extender bit_extender_7
  assign out_10 = {{3{1'b0}}, Input[7]};  // Bit_Extender bit_extender_8
  assign out_9 = {{3{1'b0}}, Input[8]};  // Bit_Extender bit_extender_9
  assign out_8 = {{3{1'b0}}, Input[9]};  // Bit_Extender bit_extender_10
  assign out_7 = {{3{1'b0}}, Input[10]};  // Bit_Extender bit_extender_11
  assign out_6 = {{3{1'b0}}, Input[11]};  // Bit_Extender bit_extender_12
  assign out_5 = {{3{1'b0}}, Input[12]};  // Bit_Extender bit_extender_13
  assign out_4 = {{3{1'b0}}, Input[13]};  // Bit_Extender bit_extender_14
  assign out_3 = {{3{1'b0}}, Input[14]};  // Bit_Extender bit_extender_15
  assign mais_sign = {{3{1'b0}}, Input[15]};  // Bit_Extender bit_extender_16
endmodule

// AND
module PORT_AND (
  input  COMUM,
  input  in_1,
  input  in_2,
  input  in_3,
  input  in_4,
  input  in_5,
  input  in_6,
  input  in_7,
  input  in_8,
  input  in_9,
  input  in_10,
  input  in_11,
  input  in_12,
  input  in_13,
  input  in_14,
  output out_1,
  output out_2,
  output out_3,
  output out_4,
  output out_5,
  output out_6,
  output out_7,
  output out_8,
  output out_9,
  output out_10,
  output out_11,
  output out_12,
  output out_13,
  output out_14
);

  and and_1 (out_1, COMUM, in_1);
  and and_2 (out_2, COMUM, in_2);
  and and_3 (out_3, COMUM, in_3);
  and and_4 (out_4, COMUM, in_4);
  and and_5 (out_5, COMUM, in_5);
  and and_6 (out_6, COMUM, in_6);
  and and_7 (out_7, COMUM, in_7);
  and and_8 (out_8, COMUM, in_8);
  and and_9 (out_9, COMUM, in_9);
  and and_10 (out_10, COMUM, in_10);
  and and_11 (out_11, COMUM, in_11);
  and and_12 (out_12, COMUM, in_12);
  and and_13 (out_13, COMUM, in_13);
  and and_14 (out_14, COMUM, in_14);
endmodule

module CPU (
  input  CLOCK,
  input  ON_OFF,
  input  RESET,
  output [15:0] INSTRUCTION,
  output READ_MEM,
  output WRITE_MEM,
  output [7:0] S0,
  output [7:0] S1,
  output [7:0] S2,
  output [7:0] T0,
  output [7:0] T1,
  output [7:0] D0,
  output [7:0] D1
);

  wire controller_1_alu_en, controller_1_cpi_en, controller_1_mem_cl, controller_1_pc_cl, controller_1_pc_en,
       controller_1_r_cl, controller_1_r_en, controller_1_reg_en_write, controller_1_regs_cl,
       count_cpi_1_pulso, not_1_out;
  wire [2:0] controller_1_alu_op, controller_1_r1_select, controller_1_r2_select, controller_1_r_data_select;
  wire [3:0] controller_1_pc_in, PC_q, show_instr_1_mais_sign, show_instr_1_menos_sign, show_instr_1_out_3,
       show_instr_1_out_4, show_instr_1_out_5, show_instr_1_out_6, show_instr_1_out_7, show_instr_1_out_8,
       show_instr_1_out_9, show_instr_1_out_10, show_instr_1_out_11, show_instr_1_out_12,
       show_instr_1_out_13, show_instr_1_out_14, show_instr_1_out_15, show_instr_1_out_16;
  wire [6:0] bit_extender_1_out;
  wire [7:0] alu_1_out, controlled_buffer_1_out, controlled_buffer_2_out, controller_1_alu_a,
       controller_1_alu_b, controller_1_mem_data_adrress, controller_1_reg_data, controller_1_write_mem_data,
       regiters_show_1_out_1, regiters_show_1_out_2;
  wire [15:0] rom_1_data;

  COUNT_CPI count_cpi_1 (.PULSO(count_cpi_1_pulso), .Enable(controller_1_cpi_en), .Clock(CLOCK));  // open: Clear
  CONTROLLER controller_1 (
    .pc_en(controller_1_pc_en), .pc_cl(controller_1_pc_cl), .r_en(controller_1_r_en),
    .r_cl(controller_1_r_cl), .data_instr(INSTRUCTION), .mem_data_adrress(controller_1_mem_data_adrress),
    .mem_s_r(READ_MEM), .mem_cl(controller_1_mem_cl), .load_mem_data(controlled_buffer_2_out),
    .on_off(ON_OFF), .Reset(RESET), .r1_select(controller_1_r1_select), .r2_select(controller_1_r2_select),
    .r_data_select(controller_1_r_data_select), .REG_DATA(controller_1_reg_data),
    .regs_cl(controller_1_regs_cl), .r1_out(regiters_show_1_out_1), .r2_out(regiters_show_1_out_2),
    .alu_a(controller_1_alu_a), .alu_b(controller_1_alu_b), .alu_op(controller_1_alu_op),
    .alu_en(controller_1_alu_en), .alu_out(alu_1_out), .pc_out(PC_q), .pc_in(controller_1_pc_in),
    .REG_EN_WRITE(controller_1_reg_en_write), .CLOCK(CLOCK), .cpi_en(controller_1_cpi_en),
    .write_mem_data(controller_1_write_mem_data));
  Hex_Digit_Display hex_digit_display_1 (.value(show_instr_1_out_3));  // open: dp
  Hex_Digit_Display hex_digit_display_2 (.value(show_instr_1_mais_sign));  // open: dp
  SHOW_INSTR show_instr_1 (
    .Input(INSTRUCTION), .mais_sign(show_instr_1_mais_sign), .out_3(show_instr_1_out_3),
    .out_4(show_instr_1_out_4), .out_5(show_instr_1_out_5), .out_6(show_instr_1_out_6),
    .out_7(show_instr_1_out_7), .out_8(show_instr_1_out_8), .out_9(show_instr_1_out_9),
    .out_10(show_instr_1_out_10), .out_11(show_instr_1_out_11), .out_12(show_instr_1_out_12),
    .out_13(show_instr_1_out_13), .out_14(show_instr_1_out_14), .out_15(show_instr_1_out_15),
    .out_16(show_instr_1_out_16), .menos_sign(show_instr_1_menos_sign));
  Register #(.width(4)) PC (
    .D(controller_1_pc_in), .en(controller_1_pc_en), .Q(PC_q), .clk(count_cpi_1_pulso),
    .clr(controller_1_pc_cl));
  Hex_Digit_Display hex_digit_display_3 (.value(show_instr_1_out_4));  // open: dp
  REGITERS_SHOW regiters_show_1 (
    .DATA(controller_1_reg_data), .SELECT_WRITE(controller_1_r_data_select), .OUT_1(regiters_show_1_out_1),
    .SELECT_OUT_1(controller_1_r1_select), .OUT_2(regiters_show_1_out_2),
    .SELECT_OUT_2(controller_1_r2_select), .CLOCK(CLOCK), .ENABLE(controller_1_reg_en_write),
    .CLEAR(controller_1_regs_cl), .D1(D1), .D0(D0), .T1(T1), .T0(T0), .S2(S2), .S1(S1), .S0(S0));
  Hex_Digit_Display hex_digit_display_4 (.value(show_instr_1_out_5));  // open: dp
  Hex_Digit_Display hex_digit_display_5 (.value(show_instr_1_out_6));  // open: dp
  Register #(.width(16)) register_1 (
    .D(rom_1_data), .en(controller_1_r_en), .Q(INSTRUCTION), .clk(CLOCK), .clr(controller_1_r_cl));
  ROM #(.addrWidth(4), .dataWidth(16)) rom_1 (.addr(PC_q), .data(rom_1_data));  // open: sel
  Hex_Digit_Display hex_digit_display_6 (.value(show_instr_1_out_8));  // open: dp
  Hex_Digit_Display hex_digit_display_7 (.value(show_instr_1_out_7));  // open: dp
  Hex_Digit_Display hex_digit_display_8 (.value(show_instr_1_out_10));  // open: dp
  Hex_Digit_Display hex_digit_display_9 (.value(show_instr_1_out_9));  // open: dp
  Hex_Digit_Display hex_digit_display_10 (.value(show_instr_1_out_12));  // open: dp
  Hex_Digit_Display hex_digit_display_11 (.value(show_instr_1_out_11));  // open: dp
  Bit_Extender #(.out_width(7)) bit_extender_1 (.in(controller_1_mem_data_adrress), .out(bit_extender_1_out));
  ALU alu_1 (
    .IN_A(controller_1_alu_a), .IN_B(controller_1_alu_b), .OUT(alu_1_out), .Select(controller_1_alu_op),
    .Enable(controller_1_alu_en));
  Hex_Digit_Display hex_digit_display_12 (.value(show_instr_1_out_13));  // open: dp
  Hex_Digit_Display hex_digit_display_13 (.value(show_instr_1_out_14));  // open: dp
  Hex_Digit_Display hex_digit_display_14 (.value(show_instr_1_out_16));  // open: dp
  Hex_Digit_Display hex_digit_display_15 (.value(show_instr_1_out_15));  // open: dp
  assign controlled_buffer_1_out = not_1_out ? controller_1_write_mem_data : 8'bz;  // Controlled_Buffer controlled_buffer_1
  RAM #(.addrWidth(7)) ram_1 (
    .addr(bit_extender_1_out), .data(controlled_buffer_1_out), .clk(CLOCK), .ld(READ_MEM),
    .clr(controller_1_mem_cl));  // open: sel
  not not_1 (not_1_out, READ_MEM);
  Hex_Digit_Display hex_digit_display_16 (.value(show_instr_1_menos_sign));  // open: dp
  assign controlled_buffer_2_out = READ_MEM ? controlled_buffer_1_out : 8'bz;  // Controlled_Buffer controlled_buffer_2
  not not_2 (WRITE_MEM, READ_MEM);

  // Other names for the same wires on the sheet: INSTR[15:0] = INSTRUCTION

  // Notes on the sheet:
  //   contents of rom_1 (hex, n*v repeats v):
  //   c08a c200 c381 d201 50e7 bf03 e006
endmodule

module LEDS (
  input  in_1,
  input  in_2,
  input  ON_OFF,
  input  in_4,
  input  in_5,
  input  Enable,
  input  Clear,
  input  Enable_2,
  input  Clear_2,
  input  [6:0] in_10,
  input  [6:0] in_11,
  input  [6:0] in_12,
  input  Clock,
  input  Clock_2,
  input  Enable_3,
  input  Clock_3,
  output [6:0] out_17,
  output out_18,
  output PULSO,
  output PULSO_2,
  output Clear_3,
  output PULSO_3
);

  wire adder_1_out, clock_2_out, clock_out, controller_1_alu_en, controller_1_cpi_en, controller_1_mem_cl,
       controller_1_mem_s_r, controller_1_pc_cl, controller_1_pc_en, controller_1_r_cl, controller_1_r_en,
       controller_1_reg_en_write, controller_1_regs_cl, count_cpi_1_pulso, not_1_out, not_2_out,
       register_2_q, RESET_out, undriven;
  wire [1:0] adder_2_out, adder_3_out, register_3_q, register_4_q;
  wire [2:0] controller_1_alu_op, controller_1_r1_select, controller_1_r2_select, controller_1_r_data_select;
  wire [3:0] controller_1_pc_in, PC_q, show_instr_1_mais_sign, show_instr_1_menos_sign, show_instr_1_out_3,
       show_instr_1_out_4, show_instr_1_out_5, show_instr_1_out_6, show_instr_1_out_7, show_instr_1_out_8,
       show_instr_1_out_9, show_instr_1_out_10, show_instr_1_out_11, show_instr_1_out_12,
       show_instr_1_out_13, show_instr_1_out_14, show_instr_1_out_15, show_instr_1_out_16;
  wire [6:0] bit_extender_1_out, keyboard_2_data;
  wire [7:0] alu_1_out, controller_1_alu_a, controller_1_alu_b, controller_1_mem_data_adrress,
       controller_1_reg_data, ram_1_data, registers_1_out_1, registers_1_out_2;
  wire [15:0] INSTR, rom_1_data;

  Button RESET (.out(RESET_out));
  COUNT_CPI count_cpi_1 (.PULSO(count_cpi_1_pulso), .Enable(controller_1_cpi_en), .Clock(clock_out));  // open: Clear
  CONTROLLER controller_1 (
    .pc_en(controller_1_pc_en), .pc_cl(controller_1_pc_cl), .r_en(controller_1_r_en),
    .r_cl(controller_1_r_cl), .data_instr(INSTR), .mem_data_adrress(controller_1_mem_data_adrress),
    .mem_s_r(controller_1_mem_s_r), .mem_cl(controller_1_mem_cl), .on_off(ON_OFF), .Reset(RESET_out),
    .r1_select(controller_1_r1_select), .r2_select(controller_1_r2_select),
    .r_data_select(controller_1_r_data_select), .REG_DATA(controller_1_reg_data),
    .regs_cl(controller_1_regs_cl), .r1_out(registers_1_out_1), .r2_out(registers_1_out_2),
    .alu_a(controller_1_alu_a), .alu_b(controller_1_alu_b), .alu_op(controller_1_alu_op),
    .alu_en(controller_1_alu_en), .alu_out(alu_1_out), .pc_out(PC_q), .pc_in(controller_1_pc_in),
    .REG_EN_WRITE(controller_1_reg_en_write), .CLOCK(clock_out), .cpi_en(controller_1_cpi_en));  // open: load_mem_data, write_mem_data
  Hex_Digit_Display hex_digit_display_1 (.value(show_instr_1_out_3));  // open: dp
  Hex_Digit_Display hex_digit_display_2 (.value(show_instr_1_mais_sign));  // open: dp
  SHOW_INSTR show_instr_1 (
    .Input(INSTR), .mais_sign(show_instr_1_mais_sign), .out_3(show_instr_1_out_3),
    .out_4(show_instr_1_out_4), .out_5(show_instr_1_out_5), .out_6(show_instr_1_out_6),
    .out_7(show_instr_1_out_7), .out_8(show_instr_1_out_8), .out_9(show_instr_1_out_9),
    .out_10(show_instr_1_out_10), .out_11(show_instr_1_out_11), .out_12(show_instr_1_out_12),
    .out_13(show_instr_1_out_13), .out_14(show_instr_1_out_14), .out_15(show_instr_1_out_15),
    .out_16(show_instr_1_out_16), .menos_sign(show_instr_1_menos_sign));
  Register #(.width(4)) PC (
    .D(controller_1_pc_in), .en(controller_1_pc_en), .Q(PC_q), .clk(count_cpi_1_pulso),
    .clr(controller_1_pc_cl));
  REGISTERS registers_1 (
    .DATA(controller_1_reg_data), .SELECT_WRITE(controller_1_r_data_select), .OUT_1(registers_1_out_1),
    .ENABLE(controller_1_reg_en_write), .CLOCK(clock_out), .CLEAR(controller_1_regs_cl),
    .OUT_2(registers_1_out_2), .SELECT_OUT_2(controller_1_r2_select), .SELECT_OUT_1(controller_1_r1_select));
  Hex_Digit_Display hex_digit_display_3 (.value(show_instr_1_out_4));  // open: dp
  Hex_Digit_Display hex_digit_display_4 (.value(show_instr_1_out_6));  // open: dp
  Hex_Digit_Display hex_digit_display_5 (.value(show_instr_1_out_5));  // open: dp
  Register #(.width(16)) register_1 (
    .D(rom_1_data), .en(controller_1_r_en), .Q(INSTR), .clk(clock_out), .clr(controller_1_r_cl));
  ROM #(.addrWidth(4), .dataWidth(16)) rom_1 (.addr(PC_q), .data(rom_1_data));  // open: sel
  Hex_Digit_Display hex_digit_display_6 (.value(show_instr_1_out_8));  // open: dp
  Hex_Digit_Display hex_digit_display_7 (.value(show_instr_1_out_7));  // open: dp
  Hex_Digit_Display hex_digit_display_8 (.value(show_instr_1_out_10));  // open: dp
  Hex_Digit_Display hex_digit_display_9 (.value(show_instr_1_out_9));  // open: dp
  Hex_Digit_Display hex_digit_display_10 (.value(show_instr_1_out_11));  // open: dp
  Hex_Digit_Display hex_digit_display_11 (.value(show_instr_1_out_12));  // open: dp
  Bit_Extender #(.out_width(7)) bit_extender_1 (.in(controller_1_mem_data_adrress), .out(bit_extender_1_out));
  ALU alu_1 (
    .IN_A(controller_1_alu_a), .IN_B(controller_1_alu_b), .OUT(alu_1_out), .Select(controller_1_alu_op),
    .Enable(controller_1_alu_en));
  Hex_Digit_Display hex_digit_display_12 (.value(show_instr_1_out_14));  // open: dp
  Hex_Digit_Display hex_digit_display_13 (.value(show_instr_1_out_13));  // open: dp
  Adder #(.width(1)) adder_1 (.a(register_2_q), .b(1'b1), .out(adder_1_out), .cout(PULSO_2));  // open: cin
  Hex_Digit_Display hex_digit_display_14 (.value(show_instr_1_out_16));  // open: dp
  Hex_Digit_Display hex_digit_display_15 (.value(show_instr_1_out_15));  // open: dp
  RAM #(.addrWidth(7)) ram_1 (
    .addr(bit_extender_1_out), .data(ram_1_data), .clk(clock_out), .ld(controller_1_mem_s_r),
    .clr(controller_1_mem_cl));  // open: sel
  Register #(.width(1)) register_2 (.D(adder_1_out), .en(Enable_2), .Q(register_2_q), .clk(Clock_2), .clr(Clear_2));
  Hex_Digit_Display hex_digit_display_16 (.value(show_instr_1_menos_sign));  // open: dp
  LED READ (.in(controller_1_mem_s_r));
  LED WRITE (.in(not_1_out));
  not not_1 (not_1_out, controller_1_mem_s_r);
  Clock u_clock (.out(clock_out));
  Adder #(.width(2)) adder_2 (.a(register_3_q), .b(2'b01), .out(adder_2_out), .cout(PULSO));  // open: cin
  Multiplexer #(.width(2), .enable("false")) multiplexer_1 (.in0(2'b01), .in1(2'b10), .sel(undriven));  // open: out
  Register #(.width(2)) register_3 (.D(adder_2_out), .en(Enable), .Q(register_3_q), .clk(Clock), .clr(Clear));
  Keyboard keyboard_1 (.clk(clock_2_out), .re(clock_2_out), .clr(in_1), .data(out_17));  // open: avail
  Clock u_clock_2 (.out(clock_2_out));
  Adder #(.width(2)) adder_3 (.a(register_4_q), .b(2'b01), .out(adder_3_out), .cout(PULSO_3));  // open: cin
  Register #(.width(2)) register_4 (.D(adder_3_out), .en(Enable_3), .Q(register_4_q), .clk(Clock_3), .clr(Clear_3));
  not not_2 (not_2_out, Clock_3);
  assign Clear_3 = PULSO_3 ? not_2_out : 1'bz;  // Controlled_Buffer controlled_buffer_1
  TTY tty_1 (.data(keyboard_2_data), .clk(clock_2_out), .we(in_4), .clr(in_2));
  Keyboard keyboard_2 (.clk(clock_2_out), .re(clock_2_out), .clr(in_5), .avail(out_18), .data(keyboard_2_data));
  DotMatrix dotmatrix_1 (.col0(in_10), .col1(in_11), .col2(in_12));  // open: col3, col4

  // Notes on the sheet:
  //   contents of rom_1 (hex, n*v repeats v):
  //   c081 c102 c183 c204 c285 c306 c387 e007
endmodule

// CPI
module COUNT_CPI (
  input  Enable,
  input  Clear,
  input  Clock,
  output PULSO
);

  wire [1:0] adder_1_out, register_1_q;

  Adder #(.width(2)) adder_1 (.a(register_1_q), .b(2'b01), .out(adder_1_out), .cout(PULSO));  // open: cin
  Register #(.width(2)) register_1 (.D(adder_1_out), .en(Enable), .Q(register_1_q), .clk(Clock), .clr(Clear));
endmodule

// RESGISTERS
module REGITERS_SHOW (
  input  [7:0] DATA,
  input  CLOCK,
  input  CLEAR,
  input  [2:0] SELECT_OUT_1,
  input  [2:0] SELECT_OUT_2,
  input  ENABLE,
  input  [2:0] SELECT_WRITE,
  output [7:0] D1,
  output [7:0] D0,
  output [7:0] T1,
  output [7:0] T0,
  output [7:0] S2,
  output [7:0] S1,
  output [7:0] S0,
  output [7:0] OUT_1,
  output [7:0] OUT_2
);

  wire demultiplexer_2_out0, demultiplexer_2_out1, demultiplexer_2_out2, demultiplexer_2_out3,
       demultiplexer_2_out4, demultiplexer_2_out5, demultiplexer_2_out6, demultiplexer_2_out7;
  wire [7:0] demultiplexer_1_out1, demultiplexer_1_out2, demultiplexer_1_out3, demultiplexer_1_out4,
       demultiplexer_1_out5, demultiplexer_1_out6, demultiplexer_1_out7, register_8_q;

  Demultiplexer #(.select(3), .width(8)) demultiplexer_1 (
    .out1(demultiplexer_1_out1), .out2(demultiplexer_1_out2), .out3(demultiplexer_1_out3),
    .out4(demultiplexer_1_out4), .out5(demultiplexer_1_out5), .out6(demultiplexer_1_out6),
    .out7(demultiplexer_1_out7), .in(DATA), .sel(SELECT_WRITE), .en(1'b1));  // open: out0
  Demultiplexer #(.select(3)) demultiplexer_2 (
    .out0(demultiplexer_2_out0), .out1(demultiplexer_2_out1), .out2(demultiplexer_2_out2),
    .out3(demultiplexer_2_out3), .out4(demultiplexer_2_out4), .out5(demultiplexer_2_out5),
    .out6(demultiplexer_2_out6), .out7(demultiplexer_2_out7), .in(ENABLE), .sel(SELECT_WRITE), .en(1'b1));
  Register register_1 (.D(demultiplexer_1_out7), .en(demultiplexer_2_out7), .Q(D1), .clk(CLOCK), .clr(CLEAR));
  Register register_2 (.D(demultiplexer_1_out6), .en(demultiplexer_2_out6), .Q(D0), .clk(CLOCK), .clr(CLEAR));
  Register register_3 (.D(demultiplexer_1_out5), .en(demultiplexer_2_out5), .Q(T1), .clk(CLOCK), .clr(CLEAR));
  Register register_4 (.D(demultiplexer_1_out4), .en(demultiplexer_2_out4), .Q(T0), .clk(CLOCK), .clr(CLEAR));
  Register register_5 (.D(demultiplexer_1_out3), .en(demultiplexer_2_out3), .Q(S2), .clk(CLOCK), .clr(CLEAR));
  Register register_6 (.D(demultiplexer_1_out2), .en(demultiplexer_2_out2), .Q(S1), .clk(CLOCK), .clr(CLEAR));
  Register register_7 (.D(demultiplexer_1_out1), .en(demultiplexer_2_out1), .Q(S0), .clk(CLOCK), .clr(CLEAR));
  Register register_8 (.D({8{1'b0}}), .en(demultiplexer_2_out0), .Q(register_8_q), .clk(CLOCK), .clr(CLEAR));
  Multiplexer #(.select(3), .width(8)) multiplexer_1 (
    .in0(register_8_q), .in1(S0), .in2(S1), .in3(S2), .in4(T0), .in5(T1), .in6(D0), .in7(D1), .out(OUT_1),
    .sel(SELECT_OUT_1), .en(1'b1));
  Multiplexer #(.select(3), .width(8)) multiplexer_2 (
    .in0(register_8_q), .in1(S0), .in2(S1), .in3(S2), .in4(T0), .in5(T1), .in6(D0), .in7(D1), .out(OUT_2),
    .sel(SELECT_OUT_2), .en(1'b1));
endmodule
